// Digital circuit main.dig as structural Verilog
module main (
  input  clk
);

  wire _0, _1, _2, _3, _4, _5, _6, _7, _8, _9, _10, _11, _12, _13, _14, _15, div, error, minus, mul,
       Negative, plus;
  wire [6:0] A0, A1, A2, A3, B0, B1, B2, B3, R0, R1, R2, R3;

  Seven_Seg seven_seg_1 (.a(A3[3]), .b(A3[2]), .c(A3[1]), .d(A3[0]), .e(A3[6]), .f(A3[5]), .g(A3[4]), .dp(1'b0));
  Button u__1 (.out(_1));
  Button u__4 (.out(_4));
  Button u__7 (.out(_7));
  Button C (.out(_15));
  Seven_Seg seven_seg_2 (.a(A2[3]), .b(A2[2]), .c(A2[1]), .d(A2[0]), .e(A2[6]), .f(A2[5]), .g(A2[4]), .dp(1'b0));
  Button u__2 (.out(_2));
  Button u__5 (.out(_5));
  Button u__8 (.out(_8));
  Button u__0 (.out(_0));
  Seven_Seg seven_seg_3 (.a(A1[3]), .b(A1[2]), .c(A1[1]), .d(A1[0]), .e(A1[6]), .f(A1[5]), .g(A1[4]), .dp(1'b0));
  Button u__3 (.out(_3));
  Button u__6 (.out(_6));
  Button u__9 (.out(_9));
  Button eq (.out(_14));
  Seven_Seg seven_seg_4 (.a(A0[3]), .b(A0[2]), .c(A0[1]), .d(A0[0]), .e(A0[6]), .f(A0[5]), .g(A0[4]), .dp(1'b0));
  Button u_plus (.out(_10));
  Button button (.out(_11));
  Button button_2 (.out(_12));
  Button button_3 (.out(_13));
  LED plus_2 (.in(plus));
  LED led (.in(minus));
  LED led_2 (.in(mul));
  LED led_3 (.in(div));
  Seven_Seg seven_seg_5 (.a(B3[3]), .b(B3[2]), .c(B3[1]), .d(B3[0]), .e(B3[6]), .f(B3[5]), .g(B3[4]), .dp(1'b0));
  main_embedded main_embedded_1 ();
  Seven_Seg seven_seg_6 (.a(B2[3]), .b(B2[2]), .c(B2[1]), .d(B2[0]), .e(B2[6]), .f(B2[5]), .g(B2[4]), .dp(1'b0));
  Seven_Seg seven_seg_7 (.a(B1[3]), .b(B1[2]), .c(B1[1]), .d(B1[0]), .e(B1[6]), .f(B1[5]), .g(B1[4]), .dp(1'b0));
  Seven_Seg seven_seg_8 (.a(B0[3]), .b(B0[2]), .c(B0[1]), .d(B0[0]), .e(B0[6]), .f(B0[5]), .g(B0[4]), .dp(1'b0));
  LED led_4 (.in(Negative));
  Seven_Seg seven_seg_9 (.a(R3[3]), .b(R3[2]), .c(R3[1]), .d(R3[0]), .e(R3[6]), .f(R3[5]), .g(R3[4]), .dp(1'b0));
  Seven_Seg seven_seg_10 (.a(R2[3]), .b(R2[2]), .c(R2[1]), .d(R2[0]), .e(R2[6]), .f(R2[5]), .g(R2[4]), .dp(1'b0));
  LED u_ERROR (.in(error));
  Seven_Seg seven_seg_11 (.a(R1[3]), .b(R1[2]), .c(R1[1]), .d(R1[0]), .e(R1[6]), .f(R1[5]), .g(R1[4]), .dp(1'b0));
  Seven_Seg seven_seg_12 (.a(R0[3]), .b(R0[2]), .c(R0[1]), .d(R0[0]), .e(R0[6]), .f(R0[5]), .g(R0[4]), .dp(1'b0));

  // Notes on the sheet:
  //   clk: Hz: 10
endmodule
