// Digital circuit main_embedded.dig as structural Verilog
module main_embedded (
  input  CLK,
  input  _0,
  input  _1,
  input  _2,
  input  _3,
  input  _4,
  input  _5,
  input  _6,
  input  _7,
  input  _8,
  input  _9,
  input  plus,
  input  in_31,
  input  in_32,
  input  in_33,
  input  ENTER,
  input  CLEAR,
  output ERROR,
  output [6:0] Result_3,
  output [6:0] Result_2,
  output [6:0] Result_1,
  output [6:0] Result_0,
  output NEGATIVE,
  output [6:0] NumA_3,
  output [6:0] NumA_2,
  output [6:0] NumA_1,
  output [6:0] NumA_0,
  output ADD,
  output SUB,
  output MUL,
  output DIV,
  output [6:0] NumB_3,
  output [6:0] NumB_2,
  output [6:0] NumB_1,
  output [6:0] NumB_0
);

  wire A, and_1_out, and_2_out, and_3_out, and_4_out, and_5_out, and_6_out, and_7_out, and_8_out, and_9_out,
       and_10_out, and_11_out, and_12_out, and_13_out, and_14_out, and_15_out, and_16_out, and_17_out,
       and_18_out, and_19_out, and_20_out, and_21_out, and_22_out, and_23_out, and_24_out, and_25_out,
       and_26_out, and_27_out, and_28_out, and_29_out, and_30_out, and_31_out, and_32_out, and_33_out,
       and_34_out, and_35_out, and_36_out, and_37_out, and_38_out, and_39_out, and_40_out, and_41_out,
       and_42_out, and_43_out, and_44_out, and_45_out, and_46_out, and_47_out, and_48_out, and_49_out,
       and_50_out, and_51_out, and_52_out, and_53_out, and_54_out, B, comparator_1_eq, comparator_2_eq,
       comparator_3_eq, comparator_4_eq, comparator_5_eq, comparator_6_eq, comparator_7_eq, comparator_8_eq,
       comparator_9_eq, comparator_10_eq, comparator_11_eq, comparator_12_eq, comparator_13_eq,
       comparator_14_eq, comparator_15_eq, comparator_16_eq, comparator_17_eq, comparator_18_eq,
       comparator_19_eq, comparator_20_eq, comparator_21_eq, comparator_22_eq, comparator_23_eq,
       comparator_24_eq, comparator_25_eq, comparator_26_eq, comparator_27_eq, comparator_28_eq,
       comparator_29_eq, comparator_30_eq, comparator_31_eq, comparator_32_eq, comparator_33_eq,
       comparator_34_eq, comparator_35_eq, comparator_36_eq, comparator_37_eq, comparator_38_eq,
       comparator_39_eq, comparator_40_eq, comparator_41_eq, comparator_41_gt, comparator_42_gt,
       comparator_43_eq, comparator_44_eq, comparator_45_eq, comparator_46_eq, comparator_47_eq,
       comparator_48_eq, comparator_49_eq, comparator_50_eq, comparator_51_eq, comparator_52_eq,
       comparator_53_eq, comparator_54_eq, comparator_55_eq, comparator_56_eq, comparator_57_eq,
       comparator_58_eq, comparator_59_eq, comparator_60_eq, comparator_61_eq, comparator_62_eq,
       comparator_63_eq, comparator_64_eq, comparator_65_eq, comparator_66_eq, comparator_67_eq,
       comparator_68_eq, comparator_69_eq, comparator_70_eq, comparator_71_eq, comparator_72_eq,
       comparator_73_eq, comparator_74_eq, comparator_75_eq, comparator_76_eq, comparator_77_eq,
       comparator_78_eq, comparator_79_eq, comparator_80_eq, comparator_81_eq, comparator_82_eq,
       comparator_83_eq, comparator_84_eq, comparator_85_eq, comparator_86_eq, comparator_87_gt,
       comparator_88_eq, comparator_89_eq, comparator_90_eq, comparator_91_eq, comparator_92_gt,
       comparator_93_gt, comparator_94_eq, comparator_95_eq, comparator_96_eq, comparator_97_eq,
       comparator_98_gt, comparator_99_eq, comparator_100_eq, comparator_101_eq, comparator_102_eq,
       comparator_103_eq, comparator_103_lt, comparator_104_eq, comparator_108_eq, comparator_109_eq,
       comparator_110_eq, comparator_111_eq, count1, count_gt1, count_in, count_num2, count_res, delay_2_out,
       delay_3_out, delay_4_out, delay_5_out, delay_6_out, delay_7_out, delay_9_out, delay_10_out,
       delay_12_out, delay_13_out, delay_14_out, not_1_out, not_2_out, not_3_out, not_4_out, not_5_out,
       not_6_out, not_7_out, not_8_out, num1_zero, num2_zero, or_3_out, or_4_out, or_7_out, or_8_out,
       or_9_out, or_10_out, or_11_out, or_17_out, or_19_out, or_20_out, or_22_out, or_24_out, or_26_out,
       or_30_out, or_31_out, or_32_out, or_33_out, or_34_out, or_35_out, or_36_out, or_37_out, or_39_out,
       or_41_out, or_43_out, press_notzero, register_7_q, register_48_q, relay_41_p3, relay_86_p4,
       relay_95_p4, relay_96_p4, relaydt_2_p5, relaydt_4_p5, rs_ff_as_1_nq, rs_ff_as_1_q, rs_ff_as_2_nq,
       rs_ff_as_2_q, rs_ff_as_3_nq, rs_ff_as_3_q, rs_ff_as_4_nq, rs_ff_as_4_q, rs_ff_as_5_q, rs_ff_as_6_q;
  wire [2:0] operation, relay_62_p5, relay_63_p3, relay_64_p3, relay_65_p2;
  wire [3:0] Adig0, Adig1, Adig2, Adig3, Bdig0, Bdig1, Bdig2, Bdig3, count_out, counter_2_out, delay_8_out,
       delay_11_out, numA_count, numB_count, rdigit0, rdigit1, rdigit2, rdigit3, relay_1_p5, relay_2_p3,
       relay_3_p3, relay_4_p3, relay_5_p3, relay_6_p3, relay_7_p3, relay_8_p3, relay_9_p3, relay_10_p2,
       relay_11_p5, relay_12_p3, relay_13_p3, relay_14_p3, relay_15_p3, relay_16_p3, relay_17_p3,
       relay_18_p3, relay_19_p3, relay_20_p2, relay_21_p5, relay_22_p3, relay_23_p3, relay_24_p3,
       relay_25_p3, relay_26_p3, relay_27_p3, relay_28_p3, relay_29_p3, relay_30_p2, relay_31_p5,
       relay_32_p3, relay_33_p3, relay_34_p3, relay_35_p3, relay_36_p3, relay_37_p3, relay_38_p3,
       relay_39_p3, relay_40_p2, relay_42_p5, relay_43_p3, relay_44_p3, relay_45_p3, relay_46_p3,
       relay_47_p3, relay_48_p3, relay_49_p3, relay_50_p3, relay_51_p2, relay_52_p5, relay_53_p3,
       relay_54_p3, relay_55_p3, relay_56_p3, relay_57_p3, relay_58_p3, relay_59_p3, relay_60_p3,
       relay_61_p2, relay_66_p5, relay_67_p3, relay_68_p3, relay_69_p3, relay_70_p3, relay_71_p3,
       relay_72_p3, relay_73_p3, relay_74_p3, relay_75_p2, relay_76_p5, relay_77_p3, relay_78_p3,
       relay_79_p3, relay_80_p3, relay_81_p3, relay_82_p3, relay_83_p3, relay_84_p3, relay_85_p2,
       relaydt_1_p5, relaydt_3_p5;
  wire [6:0] A0, A1, A2, A3, A4, A5, A6, A7, A8, A9, B0, B1, B2, B3, B4, B5, B6, B7, B8, B9, Num1_0, Num1_1,
       Num1_2, Num1_3, Num2_0, Num2_1, Num2_2, Num2_3, register_8_q, register_9_q, register_10_q,
       register_11_q, register_12_q, register_13_q, register_14_q, register_15_q, register_16_q,
       register_17_q, register_18_q, register_19_q, register_20_q, register_21_q, register_22_q,
       register_23_q, register_24_q, register_25_q, register_26_q, register_27_q, register_28_q,
       register_29_q, register_30_q, register_31_q, register_32_q, register_33_q, register_34_q,
       register_35_q, register_36_q, register_37_q, register_38_q, register_39_q, register_40_q,
       register_41_q, register_42_q, register_43_q, register_44_q, register_45_q, register_46_q,
       register_47_q, register_49_q, register_50_q, register_51_q, register_52_q, register_53_q,
       register_54_q, register_55_q, register_56_q, register_57_q, register_58_q, register_59_q,
       register_60_q, register_61_q, register_62_q, register_63_q, register_64_q, register_65_q,
       register_66_q, register_67_q, register_68_q, register_69_q, register_70_q, register_71_q,
       register_72_q, register_73_q, register_74_q, register_75_q, register_76_q, register_77_q,
       register_78_q, register_79_q, register_80_q, register_81_q, register_82_q, register_83_q,
       register_84_q, register_85_q, register_86_q, register_87_q, register_88_q, register_89_q,
       register_90_q;
  wire [7:0] counter_1_out;

  Comparator #(.Bits(7)) comparator_1 (.a(NumA_3), .b(7'b1101111), .eq(comparator_1_eq));  // open: gt, lt
  Comparator #(.Bits(7)) comparator_2 (.a(NumA_3), .b(7'b0000110), .eq(comparator_2_eq));  // open: gt, lt
  Comparator #(.Bits(7)) comparator_3 (.a(NumA_3), .b(7'b1011101), .eq(comparator_3_eq));  // open: gt, lt
  Comparator #(.Bits(7)) comparator_4 (.a(NumA_3), .b(7'b0011111), .eq(comparator_4_eq));  // open: gt, lt
  Comparator #(.Bits(7)) comparator_5 (.a(NumA_3), .b(7'b0110110), .eq(comparator_5_eq));  // open: gt, lt
  Comparator #(.Bits(7)) comparator_6 (.a(NumA_3), .b(7'b0111011), .eq(comparator_6_eq));  // open: gt, lt
  Comparator #(.Bits(7)) comparator_7 (.a(NumA_3), .b(7'b1110011), .eq(comparator_7_eq));  // open: gt, lt
  Comparator #(.Bits(7)) comparator_8 (.a(NumA_3), .b(7'b0001110), .eq(comparator_8_eq));  // open: gt, lt
  Comparator #(.Bits(7)) comparator_9 (.a(NumA_3), .b({7{1'b1}}), .eq(comparator_9_eq));  // open: gt, lt
  Comparator #(.Bits(7)) comparator_10 (.a(NumA_3), .b(7'b0111110), .eq(comparator_10_eq));  // open: gt, lt
  Comparator #(.Bits(7)) comparator_11 (.a(NumB_3), .b(7'b1101111), .eq(comparator_11_eq));  // open: gt, lt
  Comparator #(.Bits(7)) comparator_12 (.a(NumB_3), .b(7'b0000110), .eq(comparator_12_eq));  // open: gt, lt
  Comparator #(.Bits(7)) comparator_13 (.a(NumB_3), .b(7'b1011101), .eq(comparator_13_eq));  // open: gt, lt
  Comparator #(.Bits(7)) comparator_14 (.a(NumB_3), .b(7'b0011111), .eq(comparator_14_eq));  // open: gt, lt
  Comparator #(.Bits(7)) comparator_15 (.a(NumB_3), .b(7'b0110110), .eq(comparator_15_eq));  // open: gt, lt
  Comparator #(.Bits(7)) comparator_16 (.a(NumB_3), .b(7'b0111011), .eq(comparator_16_eq));  // open: gt, lt
  Comparator #(.Bits(7)) comparator_17 (.a(NumB_3), .b(7'b1110011), .eq(comparator_17_eq));  // open: gt, lt
  Comparator #(.Bits(7)) comparator_18 (.a(NumB_3), .b(7'b0001110), .eq(comparator_18_eq));  // open: gt, lt
  Comparator #(.Bits(7)) comparator_19 (.a(NumB_3), .b({7{1'b1}}), .eq(comparator_19_eq));  // open: gt, lt
  Comparator #(.Bits(7)) comparator_20 (.a(NumB_3), .b(7'b0111110), .eq(comparator_20_eq));  // open: gt, lt
  // Relay #(.Bits(4)) relay_1: pin names not known; wires that end beside it: comparator_1_eq, 4'b0000, comparator_2_eq, 1'b0, relay_1_p5, 1'b0
  // Relay #(.Bits(4)) relay_2: pin names not known; wires that end beside it: 4'b0001, comparator_3_eq, relay_2_p3, 1'b0
  // Relay #(.Bits(4)) relay_3: pin names not known; wires that end beside it: 4'b0010, comparator_4_eq, relay_3_p3, 1'b0
  // Relay #(.Bits(4)) relay_4: pin names not known; wires that end beside it: 4'b0011, comparator_5_eq, relay_4_p3, 1'b0
  // Relay #(.Bits(4)) relay_5: pin names not known; wires that end beside it: 4'b0100, comparator_6_eq, relay_5_p3, 1'b0
  // Relay #(.Bits(4)) relay_6: pin names not known; wires that end beside it: 4'b0101, comparator_7_eq, relay_6_p3, 1'b0
  // Relay #(.Bits(4)) relay_7: pin names not known; wires that end beside it: 4'b0110, comparator_8_eq, relay_7_p3, 1'b0
  // Relay #(.Bits(4)) relay_8: pin names not known; wires that end beside it: 4'b0111, comparator_9_eq, relay_8_p3, 1'b0
  // Relay #(.Bits(4)) relay_9: pin names not known; wires that end beside it: 4'b1000, comparator_10_eq, relay_9_p3, 1'b0
  // Relay #(.Bits(4)) relay_10: pin names not known; wires that end beside it: 4'b1001, relay_10_p2
  // Relay #(.Bits(4)) relay_11: pin names not known; wires that end beside it: comparator_11_eq, 4'b0000, comparator_12_eq, 1'b0, relay_11_p5, 1'b0
  // Relay #(.Bits(4)) relay_12: pin names not known; wires that end beside it: 4'b0001, comparator_13_eq, relay_12_p3, 1'b0
  // Relay #(.Bits(4)) relay_13: pin names not known; wires that end beside it: 4'b0010, comparator_14_eq, relay_13_p3, 1'b0
  // Relay #(.Bits(4)) relay_14: pin names not known; wires that end beside it: 4'b0011, comparator_15_eq, relay_14_p3, 1'b0
  // Relay #(.Bits(4)) relay_15: pin names not known; wires that end beside it: 4'b0100, comparator_16_eq, relay_15_p3, 1'b0
  // Relay #(.Bits(4)) relay_16: pin names not known; wires that end beside it: 4'b0101, comparator_17_eq, relay_16_p3, 1'b0
  // Relay #(.Bits(4)) relay_17: pin names not known; wires that end beside it: 4'b0110, comparator_18_eq, relay_17_p3, 1'b0
  // Relay #(.Bits(4)) relay_18: pin names not known; wires that end beside it: 4'b0111, comparator_19_eq, relay_18_p3, 1'b0
  // Relay #(.Bits(4)) relay_19: pin names not known; wires that end beside it: 4'b1000, comparator_20_eq, relay_19_p3, 1'b0
  // Relay #(.Bits(4)) relay_20: pin names not known; wires that end beside it: 4'b1001, relay_20_p2
  PullDown #(.Bits(4)) pulldown_1 (.out(relay_1_p5));
  PullDown #(.Bits(4)) pulldown_2 (.out(relay_2_p3));
  PullDown #(.Bits(4)) pulldown_3 (.out(relay_3_p3));
  PullDown #(.Bits(4)) pulldown_4 (.out(relay_4_p3));
  PullDown #(.Bits(4)) pulldown_5 (.out(relay_5_p3));
  PullDown #(.Bits(4)) pulldown_6 (.out(relay_6_p3));
  PullDown #(.Bits(4)) pulldown_7 (.out(relay_7_p3));
  PullDown #(.Bits(4)) pulldown_8 (.out(relay_8_p3));
  PullDown #(.Bits(4)) pulldown_9 (.out(relay_9_p3));
  PullDown #(.Bits(4)) pulldown_10 (.out(relay_10_p2));
  PullDown #(.Bits(4)) pulldown_11 (.out(relay_11_p5));
  PullDown #(.Bits(4)) pulldown_12 (.out(relay_12_p3));
  PullDown #(.Bits(4)) pulldown_13 (.out(relay_13_p3));
  PullDown #(.Bits(4)) pulldown_14 (.out(relay_14_p3));
  PullDown #(.Bits(4)) pulldown_15 (.out(relay_15_p3));
  PullDown #(.Bits(4)) pulldown_16 (.out(relay_16_p3));
  PullDown #(.Bits(4)) pulldown_17 (.out(relay_17_p3));
  PullDown #(.Bits(4)) pulldown_18 (.out(relay_18_p3));
  PullDown #(.Bits(4)) pulldown_19 (.out(relay_19_p3));
  PullDown #(.Bits(4)) pulldown_20 (.out(relay_20_p2));
  assign Adig3 = relay_1_p5 | relay_2_p3 | relay_3_p3 | relay_4_p3 | relay_5_p3 | relay_6_p3 | relay_7_p3 | relay_8_p3 | relay_9_p3 | relay_10_p2;  // Or or_1, 4 bits wide
  assign Bdig3 = relay_11_p5 | relay_12_p3 | relay_13_p3 | relay_14_p3 | relay_15_p3 | relay_16_p3 | relay_17_p3 | relay_18_p3 | relay_19_p3 | relay_20_p2;  // Or or_2, 4 bits wide
  Comparator #(.Bits(7)) comparator_21 (.a(NumA_2), .b(7'b1101111), .eq(comparator_21_eq));  // open: gt, lt
  Comparator #(.Bits(7)) comparator_22 (.a(NumA_2), .b(7'b0000110), .eq(comparator_22_eq));  // open: gt, lt
  Comparator #(.Bits(7)) comparator_23 (.a(NumA_2), .b(7'b1011101), .eq(comparator_23_eq));  // open: gt, lt
  Comparator #(.Bits(7)) comparator_24 (.a(NumA_2), .b(7'b0011111), .eq(comparator_24_eq));  // open: gt, lt
  Comparator #(.Bits(7)) comparator_25 (.a(NumA_2), .b(7'b0110110), .eq(comparator_25_eq));  // open: gt, lt
  Comparator #(.Bits(7)) comparator_26 (.a(NumA_2), .b(7'b0111011), .eq(comparator_26_eq));  // open: gt, lt
  Comparator #(.Bits(7)) comparator_27 (.a(NumA_2), .b(7'b1110011), .eq(comparator_27_eq));  // open: gt, lt
  Comparator #(.Bits(7)) comparator_28 (.a(NumA_2), .b(7'b0001110), .eq(comparator_28_eq));  // open: gt, lt
  Comparator #(.Bits(7)) comparator_29 (.a(NumA_2), .b({7{1'b1}}), .eq(comparator_29_eq));  // open: gt, lt
  Comparator #(.Bits(7)) comparator_30 (.a(NumA_2), .b(7'b0111110), .eq(comparator_30_eq));  // open: gt, lt
  Comparator #(.Bits(7)) comparator_31 (.a(NumB_2), .b(7'b1101111), .eq(comparator_31_eq));  // open: gt, lt
  Comparator #(.Bits(7)) comparator_32 (.a(NumB_2), .b(7'b0000110), .eq(comparator_32_eq));  // open: gt, lt
  Comparator #(.Bits(7)) comparator_33 (.a(NumB_2), .b(7'b1011101), .eq(comparator_33_eq));  // open: gt, lt
  Comparator #(.Bits(7)) comparator_34 (.a(NumB_2), .b(7'b0011111), .eq(comparator_34_eq));  // open: gt, lt
  Comparator #(.Bits(7)) comparator_35 (.a(NumB_2), .b(7'b0110110), .eq(comparator_35_eq));  // open: gt, lt
  Comparator #(.Bits(7)) comparator_36 (.a(NumB_2), .b(7'b0111011), .eq(comparator_36_eq));  // open: gt, lt
  Comparator #(.Bits(7)) comparator_37 (.a(NumB_2), .b(7'b1110011), .eq(comparator_37_eq));  // open: gt, lt
  Comparator #(.Bits(7)) comparator_38 (.a(NumB_2), .b(7'b0001110), .eq(comparator_38_eq));  // open: gt, lt
  Comparator #(.Bits(7)) comparator_39 (.a(NumB_2), .b({7{1'b1}}), .eq(comparator_39_eq));  // open: gt, lt
  Comparator #(.Bits(7)) comparator_40 (.a(NumB_2), .b(7'b0111110), .eq(comparator_40_eq));  // open: gt, lt
  or or_3 (or_3_out, plus, in_31, in_32, in_33);
  // Relay #(.Bits(4)) relay_21: pin names not known; wires that end beside it: comparator_21_eq, 4'b0000, comparator_22_eq, 1'b0, relay_21_p5, 1'b0
  // Relay #(.Bits(4)) relay_22: pin names not known; wires that end beside it: 4'b0001, comparator_23_eq, relay_22_p3, 1'b0
  // Relay #(.Bits(4)) relay_23: pin names not known; wires that end beside it: 4'b0010, comparator_24_eq, relay_23_p3, 1'b0
  // Relay #(.Bits(4)) relay_24: pin names not known; wires that end beside it: 4'b0011, comparator_25_eq, relay_24_p3, 1'b0
  // Relay #(.Bits(4)) relay_25: pin names not known; wires that end beside it: 4'b0100, comparator_26_eq, relay_25_p3, 1'b0
  // Relay #(.Bits(4)) relay_26: pin names not known; wires that end beside it: 4'b0101, comparator_27_eq, relay_26_p3, 1'b0
  // Relay #(.Bits(4)) relay_27: pin names not known; wires that end beside it: 4'b0110, comparator_28_eq, relay_27_p3, 1'b0
  // Relay #(.Bits(4)) relay_28: pin names not known; wires that end beside it: 4'b0111, comparator_29_eq, relay_28_p3, 1'b0
  // Relay #(.Bits(4)) relay_29: pin names not known; wires that end beside it: 4'b1000, comparator_30_eq, relay_29_p3, 1'b0
  // Relay #(.Bits(4)) relay_30: pin names not known; wires that end beside it: 4'b1001, relay_30_p2
  // Relay #(.Bits(4)) relay_31: pin names not known; wires that end beside it: comparator_31_eq, 4'b0000, comparator_32_eq, 1'b0, relay_31_p5, 1'b0
  // Relay #(.Bits(4)) relay_32: pin names not known; wires that end beside it: 4'b0001, comparator_33_eq, relay_32_p3, 1'b0
  // Relay #(.Bits(4)) relay_33: pin names not known; wires that end beside it: 4'b0010, comparator_34_eq, relay_33_p3, 1'b0
  // Relay #(.Bits(4)) relay_34: pin names not known; wires that end beside it: 4'b0011, comparator_35_eq, relay_34_p3, 1'b0
  // Relay #(.Bits(4)) relay_35: pin names not known; wires that end beside it: 4'b0100, comparator_36_eq, relay_35_p3, 1'b0
  // Relay #(.Bits(4)) relay_36: pin names not known; wires that end beside it: 4'b0101, comparator_37_eq, relay_36_p3, 1'b0
  // Relay #(.Bits(4)) relay_37: pin names not known; wires that end beside it: 4'b0110, comparator_38_eq, relay_37_p3, 1'b0
  // Relay #(.Bits(4)) relay_38: pin names not known; wires that end beside it: 4'b0111, comparator_39_eq, relay_38_p3, 1'b0
  // Relay #(.Bits(4)) relay_39: pin names not known; wires that end beside it: 4'b1000, comparator_40_eq, relay_39_p3, 1'b0
  // Relay #(.Bits(4)) relay_40: pin names not known; wires that end beside it: 4'b1001, relay_40_p2
  or or_4 (or_4_out, or_3_out, CLEAR);
  PullDown #(.Bits(4)) pulldown_21 (.out(relay_21_p5));
  PullDown #(.Bits(4)) pulldown_22 (.out(relay_22_p3));
  PullDown #(.Bits(4)) pulldown_23 (.out(relay_23_p3));
  PullDown #(.Bits(4)) pulldown_24 (.out(relay_24_p3));
  PullDown #(.Bits(4)) pulldown_25 (.out(relay_25_p3));
  PullDown #(.Bits(4)) pulldown_26 (.out(relay_26_p3));
  PullDown #(.Bits(4)) pulldown_27 (.out(relay_27_p3));
  PullDown #(.Bits(4)) pulldown_28 (.out(relay_28_p3));
  PullDown #(.Bits(4)) pulldown_29 (.out(relay_29_p3));
  PullDown #(.Bits(4)) pulldown_30 (.out(relay_30_p2));
  PullDown #(.Bits(4)) pulldown_31 (.out(relay_31_p5));
  PullDown #(.Bits(4)) pulldown_32 (.out(relay_32_p3));
  PullDown #(.Bits(4)) pulldown_33 (.out(relay_33_p3));
  PullDown #(.Bits(4)) pulldown_34 (.out(relay_34_p3));
  PullDown #(.Bits(4)) pulldown_35 (.out(relay_35_p3));
  PullDown #(.Bits(4)) pulldown_36 (.out(relay_36_p3));
  PullDown #(.Bits(4)) pulldown_37 (.out(relay_37_p3));
  PullDown #(.Bits(4)) pulldown_38 (.out(relay_38_p3));
  PullDown #(.Bits(4)) pulldown_39 (.out(relay_39_p3));
  PullDown #(.Bits(4)) pulldown_40 (.out(relay_40_p2));
  and and_1 (and_1_out, B, count_gt1);
  Counter #(.Bits(8)) counter_1 (.en(1'b1), .C(or_4_out), .clr(CLEAR), .out(counter_1_out));  // open: ovf
  Comparator #(.Bits(4)) comparator_41 (
    .a(count_out), .b(4'b0001), .gt(comparator_41_gt), .eq(comparator_41_eq));  // open: lt
  Comparator #(.Bits(8)) comparator_42 (.a(8'h1), .b(counter_1_out), .gt(comparator_42_gt));  // open: eq, lt
  assign Adig2 = relay_21_p5 | relay_22_p3 | relay_23_p3 | relay_24_p3 | relay_25_p3 | relay_26_p3 | relay_27_p3 | relay_28_p3 | relay_29_p3 | relay_30_p2;  // Or or_5, 4 bits wide
  assign Bdig2 = relay_31_p5 | relay_32_p3 | relay_33_p3 | relay_34_p3 | relay_35_p3 | relay_36_p3 | relay_37_p3 | relay_38_p3 | relay_39_p3 | relay_40_p2;  // Or or_6, 4 bits wide
  or or_7 (or_7_out, comparator_41_gt, comparator_41_eq);
  // Relay relay_41: pin names not known; wires that end beside it: ENTER, and_1_out, relay_41_p3, 1'b0
  PullDown pulldown_41 (.out(relay_41_p3));
  Delay #(.delayTime(2)) delay_1 (.in(or_7_out), .out(count_gt1));
  and and_2 (and_2_out, count_gt1, plus);
  and and_3 (and_3_out, count_gt1, comparator_42_gt, in_31);
  and and_4 (and_4_out, count_gt1, comparator_42_gt, in_32);
  and and_5 (and_5_out, count_gt1, comparator_42_gt, in_33);
  operation #(.applicationType("IVERILOG")) u_operation (
    .numA0(Adig0), .numA1(Adig1), .numA2(Adig2), .numA3(Adig3), .numB0(Bdig0), .numB1(Bdig1), .numB2(Bdig2),
    .numB3(Bdig3), .operation(operation), .enter(relay_41_p3), .clr(CLEAR), .error(ERROR), .result3(rdigit3),
    .result2(rdigit2), .result1(rdigit1), .result0(rdigit0), .negative(NEGATIVE));
  Comparator comparator_43 (.a(and_2_out), .b(1'b1), .eq(comparator_43_eq));  // open: gt, lt
  Comparator comparator_44 (.a(and_3_out), .b(1'b1), .eq(comparator_44_eq));  // open: gt, lt
  Comparator comparator_45 (.a(and_4_out), .b(1'b1), .eq(comparator_45_eq));  // open: gt, lt
  Comparator comparator_46 (.a(and_5_out), .b(1'b1), .eq(comparator_46_eq));  // open: gt, lt
  Comparator #(.Bits(7)) comparator_47 (.a(NumA_1), .b(7'b1101111), .eq(comparator_47_eq));  // open: gt, lt
  Comparator #(.Bits(7)) comparator_48 (.a(NumA_1), .b(7'b0000110), .eq(comparator_48_eq));  // open: gt, lt
  Comparator #(.Bits(7)) comparator_49 (.a(NumA_1), .b(7'b1011101), .eq(comparator_49_eq));  // open: gt, lt
  Comparator #(.Bits(7)) comparator_50 (.a(NumA_1), .b(7'b0011111), .eq(comparator_50_eq));  // open: gt, lt
  Comparator #(.Bits(7)) comparator_51 (.a(NumA_1), .b(7'b0110110), .eq(comparator_51_eq));  // open: gt, lt
  Comparator #(.Bits(7)) comparator_52 (.a(NumA_1), .b(7'b0111011), .eq(comparator_52_eq));  // open: gt, lt
  Comparator #(.Bits(7)) comparator_53 (.a(NumA_1), .b(7'b1110011), .eq(comparator_53_eq));  // open: gt, lt
  Comparator #(.Bits(7)) comparator_54 (.a(NumA_1), .b(7'b0001110), .eq(comparator_54_eq));  // open: gt, lt
  Comparator #(.Bits(7)) comparator_55 (.a(NumA_1), .b({7{1'b1}}), .eq(comparator_55_eq));  // open: gt, lt
  Comparator #(.Bits(7)) comparator_56 (.a(NumA_1), .b(7'b0111110), .eq(comparator_56_eq));  // open: gt, lt
  Comparator #(.Bits(7)) comparator_57 (.a(NumB_1), .b(7'b1101111), .eq(comparator_57_eq));  // open: gt, lt
  Comparator #(.Bits(7)) comparator_58 (.a(NumB_1), .b(7'b0000110), .eq(comparator_58_eq));  // open: gt, lt
  Comparator #(.Bits(7)) comparator_59 (.a(NumB_1), .b(7'b1011101), .eq(comparator_59_eq));  // open: gt, lt
  Comparator #(.Bits(7)) comparator_60 (.a(NumB_1), .b(7'b0011111), .eq(comparator_60_eq));  // open: gt, lt
  Comparator #(.Bits(7)) comparator_61 (.a(NumB_1), .b(7'b0110110), .eq(comparator_61_eq));  // open: gt, lt
  Comparator #(.Bits(7)) comparator_62 (.a(NumB_1), .b(7'b0111011), .eq(comparator_62_eq));  // open: gt, lt
  Comparator #(.Bits(7)) comparator_63 (.a(NumB_1), .b(7'b1110011), .eq(comparator_63_eq));  // open: gt, lt
  Comparator #(.Bits(7)) comparator_64 (.a(NumB_1), .b(7'b0001110), .eq(comparator_64_eq));  // open: gt, lt
  Comparator #(.Bits(7)) comparator_65 (.a(NumB_1), .b({7{1'b1}}), .eq(comparator_65_eq));  // open: gt, lt
  Comparator #(.Bits(7)) comparator_66 (.a(NumB_1), .b(7'b0111110), .eq(comparator_66_eq));  // open: gt, lt
  RS_FF_AS rs_ff_as_1 (.S(comparator_43_eq), .R(CLEAR), .Q(rs_ff_as_1_q), .nQ(rs_ff_as_1_nq));
  RS_FF_AS rs_ff_as_2 (.S(comparator_44_eq), .R(CLEAR), .Q(rs_ff_as_2_q), .nQ(rs_ff_as_2_nq));
  RS_FF_AS rs_ff_as_3 (.S(comparator_45_eq), .R(CLEAR), .Q(rs_ff_as_3_q), .nQ(rs_ff_as_3_nq));
  RS_FF_AS rs_ff_as_4 (.S(comparator_46_eq), .R(CLEAR), .Q(rs_ff_as_4_q), .nQ(rs_ff_as_4_nq));
  // Relay #(.Bits(4)) relay_42: pin names not known; wires that end beside it: comparator_47_eq, 4'b0000, comparator_48_eq, 1'b0, relay_42_p5, 1'b0
  // Relay #(.Bits(4)) relay_43: pin names not known; wires that end beside it: 4'b0001, comparator_49_eq, relay_43_p3, 1'b0
  // Relay #(.Bits(4)) relay_44: pin names not known; wires that end beside it: 4'b0010, comparator_50_eq, relay_44_p3, 1'b0
  // Relay #(.Bits(4)) relay_45: pin names not known; wires that end beside it: 4'b0011, comparator_51_eq, relay_45_p3, 1'b0
  // Relay #(.Bits(4)) relay_46: pin names not known; wires that end beside it: 4'b0100, comparator_52_eq, relay_46_p3, 1'b0
  // Relay #(.Bits(4)) relay_47: pin names not known; wires that end beside it: 4'b0101, comparator_53_eq, relay_47_p3, 1'b0
  // Relay #(.Bits(4)) relay_48: pin names not known; wires that end beside it: 4'b0110, comparator_54_eq, relay_48_p3, 1'b0
  // Relay #(.Bits(4)) relay_49: pin names not known; wires that end beside it: 4'b0111, comparator_55_eq, relay_49_p3, 1'b0
  // Relay #(.Bits(4)) relay_50: pin names not known; wires that end beside it: 4'b1000, comparator_56_eq, relay_50_p3, 1'b0
  // Relay #(.Bits(4)) relay_51: pin names not known; wires that end beside it: 4'b1001, relay_51_p2
  // Relay #(.Bits(4)) relay_52: pin names not known; wires that end beside it: comparator_57_eq, 4'b0000, comparator_58_eq, 1'b0, relay_52_p5, 1'b0
  // Relay #(.Bits(4)) relay_53: pin names not known; wires that end beside it: 4'b0001, comparator_59_eq, relay_53_p3, 1'b0
  // Relay #(.Bits(4)) relay_54: pin names not known; wires that end beside it: 4'b0010, comparator_60_eq, relay_54_p3, 1'b0
  // Relay #(.Bits(4)) relay_55: pin names not known; wires that end beside it: 4'b0011, comparator_61_eq, relay_55_p3, 1'b0
  // Relay #(.Bits(4)) relay_56: pin names not known; wires that end beside it: 4'b0100, comparator_62_eq, relay_56_p3, 1'b0
  // Relay #(.Bits(4)) relay_57: pin names not known; wires that end beside it: 4'b0101, comparator_63_eq, relay_57_p3, 1'b0
  // Relay #(.Bits(4)) relay_58: pin names not known; wires that end beside it: 4'b0110, comparator_64_eq, relay_58_p3, 1'b0
  // Relay #(.Bits(4)) relay_59: pin names not known; wires that end beside it: 4'b0111, comparator_65_eq, relay_59_p3, 1'b0
  // Relay #(.Bits(4)) relay_60: pin names not known; wires that end beside it: 4'b1000, comparator_66_eq, relay_60_p3, 1'b0
  // Relay #(.Bits(4)) relay_61: pin names not known; wires that end beside it: 4'b1001, relay_61_p2
  or or_8 (or_8_out, rs_ff_as_1_nq, delay_2_out);
  Delay #(.delayTime(2)) delay_2 (.in(comparator_43_eq), .out(delay_2_out));
  or or_9 (or_9_out, rs_ff_as_2_nq, delay_3_out);
  Delay #(.delayTime(2)) delay_3 (.in(comparator_44_eq), .out(delay_3_out));
  or or_10 (or_10_out, rs_ff_as_3_nq, delay_4_out);
  Delay #(.delayTime(2)) delay_4 (.in(comparator_45_eq), .out(delay_4_out));
  or or_11 (or_11_out, rs_ff_as_4_nq, delay_5_out);
  Delay #(.delayTime(2)) delay_5 (.in(comparator_46_eq), .out(delay_5_out));
  PullDown #(.Bits(4)) pulldown_42 (.out(relay_42_p5));
  PullDown #(.Bits(4)) pulldown_43 (.out(relay_43_p3));
  PullDown #(.Bits(4)) pulldown_44 (.out(relay_44_p3));
  PullDown #(.Bits(4)) pulldown_45 (.out(relay_45_p3));
  PullDown #(.Bits(4)) pulldown_46 (.out(relay_46_p3));
  PullDown #(.Bits(4)) pulldown_47 (.out(relay_47_p3));
  PullDown #(.Bits(4)) pulldown_48 (.out(relay_48_p3));
  PullDown #(.Bits(4)) pulldown_49 (.out(relay_49_p3));
  PullDown #(.Bits(4)) pulldown_50 (.out(relay_50_p3));
  PullDown #(.Bits(4)) pulldown_51 (.out(relay_51_p2));
  PullDown #(.Bits(4)) pulldown_52 (.out(relay_52_p5));
  PullDown #(.Bits(4)) pulldown_53 (.out(relay_53_p3));
  PullDown #(.Bits(4)) pulldown_54 (.out(relay_54_p3));
  PullDown #(.Bits(4)) pulldown_55 (.out(relay_55_p3));
  PullDown #(.Bits(4)) pulldown_56 (.out(relay_56_p3));
  PullDown #(.Bits(4)) pulldown_57 (.out(relay_57_p3));
  PullDown #(.Bits(4)) pulldown_58 (.out(relay_58_p3));
  PullDown #(.Bits(4)) pulldown_59 (.out(relay_59_p3));
  PullDown #(.Bits(4)) pulldown_60 (.out(relay_60_p3));
  PullDown #(.Bits(4)) pulldown_61 (.out(relay_61_p2));
  Register register_1 (.D(rs_ff_as_1_q), .C(or_8_out), .en(1'b1), .Q(ADD));
  Register register_2 (.D(rs_ff_as_2_q), .C(or_9_out), .en(1'b1), .Q(SUB));
  Register register_3 (.D(rs_ff_as_3_q), .C(or_10_out), .en(1'b1), .Q(MUL));
  Register register_4 (.D(rs_ff_as_4_q), .C(or_11_out), .en(1'b1), .Q(DIV));
  assign Adig1 = relay_42_p5 | relay_43_p3 | relay_44_p3 | relay_45_p3 | relay_46_p3 | relay_47_p3 | relay_48_p3 | relay_49_p3 | relay_50_p3 | relay_51_p2;  // Or or_12, 4 bits wide
  assign Bdig1 = relay_52_p5 | relay_53_p3 | relay_54_p3 | relay_55_p3 | relay_56_p3 | relay_57_p3 | relay_58_p3 | relay_59_p3 | relay_60_p3 | relay_61_p2;  // Or or_13, 4 bits wide
  // Relay #(.Bits(3)) relay_62: pin names not known; wires that end beside it: ADD, 3'b001, SUB, 1'b0, relay_62_p5, 1'b0
  // Relay #(.Bits(3)) relay_63: pin names not known; wires that end beside it: 3'b010, MUL, relay_63_p3, 1'b0
  // Relay #(.Bits(3)) relay_64: pin names not known; wires that end beside it: 3'b011, DIV, relay_64_p3, 1'b0
  // Relay #(.Bits(3)) relay_65: pin names not known; wires that end beside it: 3'b100, relay_65_p2
  PullDown #(.Bits(3)) pulldown_62 (.out(relay_62_p5));
  PullDown #(.Bits(3)) pulldown_63 (.out(relay_63_p3));
  PullDown #(.Bits(3)) pulldown_64 (.out(relay_64_p3));
  PullDown #(.Bits(3)) pulldown_65 (.out(relay_65_p2));
  assign operation = relay_62_p5 | relay_63_p3 | relay_64_p3 | relay_65_p2;  // Or or_14, 3 bits wide
  Comparator #(.Bits(7)) comparator_67 (.a(NumA_0), .b(7'b1101111), .eq(comparator_67_eq));  // open: gt, lt
  Comparator #(.Bits(7)) comparator_68 (.a(NumA_0), .b(7'b0000110), .eq(comparator_68_eq));  // open: gt, lt
  Comparator #(.Bits(7)) comparator_69 (.a(NumA_0), .b(7'b1011101), .eq(comparator_69_eq));  // open: gt, lt
  Comparator #(.Bits(7)) comparator_70 (.a(NumA_0), .b(7'b0011111), .eq(comparator_70_eq));  // open: gt, lt
  Comparator #(.Bits(7)) comparator_71 (.a(NumA_0), .b(7'b0110110), .eq(comparator_71_eq));  // open: gt, lt
  Comparator #(.Bits(7)) comparator_72 (.a(NumA_0), .b(7'b0111011), .eq(comparator_72_eq));  // open: gt, lt
  Comparator #(.Bits(7)) comparator_73 (.a(NumA_0), .b(7'b1110011), .eq(comparator_73_eq));  // open: gt, lt
  Comparator #(.Bits(7)) comparator_74 (.a(NumA_0), .b(7'b0001110), .eq(comparator_74_eq));  // open: gt, lt
  Comparator #(.Bits(7)) comparator_75 (.a(NumA_0), .b({7{1'b1}}), .eq(comparator_75_eq));  // open: gt, lt
  Comparator #(.Bits(7)) comparator_76 (.a(NumA_0), .b(7'b0111110), .eq(comparator_76_eq));  // open: gt, lt
  Comparator #(.Bits(7)) comparator_77 (.a(NumB_0), .b(7'b1101111), .eq(comparator_77_eq));  // open: gt, lt
  Comparator #(.Bits(7)) comparator_78 (.a(NumB_0), .b(7'b0000110), .eq(comparator_78_eq));  // open: gt, lt
  Comparator #(.Bits(7)) comparator_79 (.a(NumB_0), .b(7'b1011101), .eq(comparator_79_eq));  // open: gt, lt
  Comparator #(.Bits(7)) comparator_80 (.a(NumB_0), .b(7'b0011111), .eq(comparator_80_eq));  // open: gt, lt
  Comparator #(.Bits(7)) comparator_81 (.a(NumB_0), .b(7'b0110110), .eq(comparator_81_eq));  // open: gt, lt
  Comparator #(.Bits(7)) comparator_82 (.a(NumB_0), .b(7'b0111011), .eq(comparator_82_eq));  // open: gt, lt
  Comparator #(.Bits(7)) comparator_83 (.a(NumB_0), .b(7'b1110011), .eq(comparator_83_eq));  // open: gt, lt
  Comparator #(.Bits(7)) comparator_84 (.a(NumB_0), .b(7'b0001110), .eq(comparator_84_eq));  // open: gt, lt
  Comparator #(.Bits(7)) comparator_85 (.a(NumB_0), .b({7{1'b1}}), .eq(comparator_85_eq));  // open: gt, lt
  Comparator #(.Bits(7)) comparator_86 (.a(NumB_0), .b(7'b0111110), .eq(comparator_86_eq));  // open: gt, lt
  // Relay #(.Bits(4)) relay_66: pin names not known; wires that end beside it: comparator_67_eq, 4'b0000, comparator_68_eq, 1'b0, relay_66_p5, 1'b0
  // Relay #(.Bits(4)) relay_67: pin names not known; wires that end beside it: 4'b0001, comparator_69_eq, relay_67_p3, 1'b0
  // Relay #(.Bits(4)) relay_68: pin names not known; wires that end beside it: 4'b0010, comparator_70_eq, relay_68_p3, 1'b0
  // Relay #(.Bits(4)) relay_69: pin names not known; wires that end beside it: 4'b0011, comparator_71_eq, relay_69_p3, 1'b0
  // Relay #(.Bits(4)) relay_70: pin names not known; wires that end beside it: 4'b0100, comparator_72_eq, relay_70_p3, 1'b0
  // Relay #(.Bits(4)) relay_71: pin names not known; wires that end beside it: 4'b0101, comparator_73_eq, relay_71_p3, 1'b0
  // Relay #(.Bits(4)) relay_72: pin names not known; wires that end beside it: 4'b0110, comparator_74_eq, relay_72_p3, 1'b0
  // Relay #(.Bits(4)) relay_73: pin names not known; wires that end beside it: 4'b0111, comparator_75_eq, relay_73_p3, 1'b0
  // Relay #(.Bits(4)) relay_74: pin names not known; wires that end beside it: 4'b1000, comparator_76_eq, relay_74_p3, 1'b0
  // Relay #(.Bits(4)) relay_75: pin names not known; wires that end beside it: 4'b1001, relay_75_p2
  // Relay #(.Bits(4)) relay_76: pin names not known; wires that end beside it: comparator_77_eq, 4'b0000, comparator_78_eq, 1'b0, relay_76_p5, 1'b0
  // Relay #(.Bits(4)) relay_77: pin names not known; wires that end beside it: 4'b0001, comparator_79_eq, relay_77_p3, 1'b0
  // Relay #(.Bits(4)) relay_78: pin names not known; wires that end beside it: 4'b0010, comparator_80_eq, relay_78_p3, 1'b0
  // Relay #(.Bits(4)) relay_79: pin names not known; wires that end beside it: 4'b0011, comparator_81_eq, relay_79_p3, 1'b0
  // Relay #(.Bits(4)) relay_80: pin names not known; wires that end beside it: 4'b0100, comparator_82_eq, relay_80_p3, 1'b0
  // Relay #(.Bits(4)) relay_81: pin names not known; wires that end beside it: 4'b0101, comparator_83_eq, relay_81_p3, 1'b0
  // Relay #(.Bits(4)) relay_82: pin names not known; wires that end beside it: 4'b0110, comparator_84_eq, relay_82_p3, 1'b0
  // Relay #(.Bits(4)) relay_83: pin names not known; wires that end beside it: 4'b0111, comparator_85_eq, relay_83_p3, 1'b0
  // Relay #(.Bits(4)) relay_84: pin names not known; wires that end beside it: 4'b1000, comparator_86_eq, relay_84_p3, 1'b0
  // Relay #(.Bits(4)) relay_85: pin names not known; wires that end beside it: 4'b1001, relay_85_p2
  PullDown #(.Bits(4)) pulldown_66 (.out(relay_66_p5));
  PullDown #(.Bits(4)) pulldown_67 (.out(relay_67_p3));
  PullDown #(.Bits(4)) pulldown_68 (.out(relay_68_p3));
  PullDown #(.Bits(4)) pulldown_69 (.out(relay_69_p3));
  PullDown #(.Bits(4)) pulldown_70 (.out(relay_70_p3));
  PullDown #(.Bits(4)) pulldown_71 (.out(relay_71_p3));
  PullDown #(.Bits(4)) pulldown_72 (.out(relay_72_p3));
  PullDown #(.Bits(4)) pulldown_73 (.out(relay_73_p3));
  PullDown #(.Bits(4)) pulldown_74 (.out(relay_74_p3));
  PullDown #(.Bits(4)) pulldown_75 (.out(relay_75_p2));
  PullDown #(.Bits(4)) pulldown_76 (.out(relay_76_p5));
  PullDown #(.Bits(4)) pulldown_77 (.out(relay_77_p3));
  PullDown #(.Bits(4)) pulldown_78 (.out(relay_78_p3));
  PullDown #(.Bits(4)) pulldown_79 (.out(relay_79_p3));
  PullDown #(.Bits(4)) pulldown_80 (.out(relay_80_p3));
  PullDown #(.Bits(4)) pulldown_81 (.out(relay_81_p3));
  PullDown #(.Bits(4)) pulldown_82 (.out(relay_82_p3));
  PullDown #(.Bits(4)) pulldown_83 (.out(relay_83_p3));
  PullDown #(.Bits(4)) pulldown_84 (.out(relay_84_p3));
  PullDown #(.Bits(4)) pulldown_85 (.out(relay_85_p2));
  assign Adig0 = relay_66_p5 | relay_67_p3 | relay_68_p3 | relay_69_p3 | relay_70_p3 | relay_71_p3 | relay_72_p3 | relay_73_p3 | relay_74_p3 | relay_75_p2;  // Or or_15, 4 bits wide
  assign Bdig0 = relay_76_p5 | relay_77_p3 | relay_78_p3 | relay_79_p3 | relay_80_p3 | relay_81_p3 | relay_82_p3 | relay_83_p3 | relay_84_p3 | relay_85_p2;  // Or or_16, 4 bits wide
  and and_6 (and_6_out, B, count_gt1);
  Seven_Seg seven_seg_1 (
    .a(NumA_3[3]), .b(NumA_3[2]), .c(NumA_3[1]), .d(NumA_3[0]), .e(NumA_3[6]), .f(NumA_3[5]), .g(NumA_3[4]),
    .dp(1'b0));
  // Relay relay_86: pin names not known; wires that end beside it: and_6_out, ENTER, 1'b0, relay_86_p4
  PullDown pulldown_86 (.out(relay_86_p4));
  not not_1 (not_1_out, ERROR);
  RS_FF_AS rs_ff_as_5 (.S(relay_86_p4), .R(CLEAR), .Q(rs_ff_as_5_q));  // open: nQ
  Seven_Seg seven_seg_2 (
    .a(NumA_2[3]), .b(NumA_2[2]), .c(NumA_2[1]), .d(NumA_2[0]), .e(NumA_2[6]), .f(NumA_2[5]), .g(NumA_2[4]),
    .dp(1'b0));
  and and_7 (and_7_out, not_1_out, rs_ff_as_5_q);
  Comparator #(.Bits(4)) comparator_87 (.a(count_out), .b(4'b0100), .gt(comparator_87_gt));  // open: eq, lt
  not not_2 (not_2_out, comparator_87_gt);
  Comparator #(.Bits(4)) comparator_88 (.a(numA_count), .b(4'b0001), .eq(comparator_88_eq));  // open: gt, lt
  Comparator #(.Bits(4)) comparator_89 (.a(numA_count), .b(4'b0010), .eq(comparator_89_eq));  // open: gt, lt
  Comparator #(.Bits(4)) comparator_90 (.a(numA_count), .b(4'b0011), .eq(comparator_90_eq));  // open: gt, lt
  Comparator #(.Bits(4)) comparator_91 (.a(numA_count), .b(4'b0100), .eq(comparator_91_eq));  // open: gt, lt
  Seven_Seg seven_seg_3 (
    .a(NumA_1[3]), .b(NumA_1[2]), .c(NumA_1[1]), .d(NumA_1[0]), .e(NumA_1[6]), .f(NumA_1[5]), .g(NumA_1[4]),
    .dp(1'b0));
  and and_8 (and_8_out, A, not_2_out);
  and and_9 (and_9_out, comparator_88_eq, 1'b1);
  and and_10 (and_10_out, comparator_89_eq, 1'b1);
  and and_11 (and_11_out, comparator_90_eq, 1'b1);
  and and_12 (and_12_out, comparator_91_eq, 1'b1);
  _7448 _7448_1 (
    .pin1(rdigit0[1]), .pin2(rdigit0[2]), .pin3(and_7_out), .pin4(and_7_out), .pin5(and_7_out),
    .pin6(rdigit0[3]), .pin7(rdigit0[0]), .pin8(1'b0), .pin9(Result_0[6]), .pin10(Result_0[0]),
    .pin11(Result_0[1]), .pin12(Result_0[2]), .pin13(Result_0[3]), .pin14(Result_0[4]), .pin15(Result_0[5]),
    .pin16(1'b1));
  _7448 _7448_2 (
    .pin1(rdigit1[1]), .pin2(rdigit1[2]), .pin3(and_7_out), .pin4(and_7_out), .pin5(and_7_out),
    .pin6(rdigit1[3]), .pin7(rdigit1[0]), .pin8(1'b0), .pin9(Result_1[6]), .pin10(Result_1[0]),
    .pin11(Result_1[1]), .pin12(Result_1[2]), .pin13(Result_1[3]), .pin14(Result_1[4]), .pin15(Result_1[5]),
    .pin16(1'b1));
  _7448 _7448_3 (
    .pin1(rdigit2[1]), .pin2(rdigit2[2]), .pin3(and_7_out), .pin4(and_7_out), .pin5(and_7_out),
    .pin6(rdigit2[3]), .pin7(rdigit2[0]), .pin8(1'b0), .pin9(Result_2[6]), .pin10(Result_2[0]),
    .pin11(Result_2[1]), .pin12(Result_2[2]), .pin13(Result_2[3]), .pin14(Result_2[4]), .pin15(Result_2[5]),
    .pin16(1'b1));
  _7448 _7448_4 (
    .pin1(rdigit3[1]), .pin2(rdigit3[2]), .pin3(and_7_out), .pin4(and_7_out), .pin5(and_7_out),
    .pin6(rdigit3[3]), .pin7(rdigit3[0]), .pin8(1'b0), .pin9(Result_3[6]), .pin10(Result_3[0]),
    .pin11(Result_3[1]), .pin12(Result_3[2]), .pin13(Result_3[3]), .pin14(Result_3[4]), .pin15(Result_3[5]),
    .pin16(1'b1));
  Delay #(.delayTime(2)) delay_6 (.in(CLEAR), .out(delay_6_out));
  Delay #(.delayTime(14)) delay_7 (.in(count_in), .out(delay_7_out));
  // Relay #(.Bits(7)) relay_87: pin names not known; wires that end beside it: and_9_out, Num1_0, and_10_out, 1'b0, NumA_0, 1'b0
  // Relay #(.poles(2), .Bits(7)) relay_88: pin names not known; wires that end beside it: Num1_0, Num1_1, NumA_1, NumA_0
  // Relay #(.poles(3), .Bits(7)) relay_89: pin names not known; wires that end beside it: and_11_out, Num1_0, Num1_1, Num1_2, 1'b0, NumA_2, NumA_1, NumA_0
  // Relay #(.poles(4), .Bits(7)) relay_90: pin names not known; wires that end beside it: and_12_out, Num1_0, Num1_1, Num1_2, Num1_3, 1'b0, NumA_3, NumA_2, NumA_1, NumA_0
  Delay #(.Bits(4), .delayTime(3)) delay_8 (.in(count_out), .out(delay_8_out));
  // RelayDT #(.Bits(4)) relaydt_1: pin names not known; wires that end beside it: CLEAR, 4'b0000, delay_8_out, 1'b0, relaydt_1_p5
  Register #(.Bits(4)) register_5 (.D(relaydt_1_p5), .C(relaydt_2_p5), .en(and_8_out), .Q(numA_count));
  // RelayDT relaydt_2: pin names not known; wires that end beside it: delay_6_out, CLEAR, delay_7_out, 1'b0, relaydt_2_p5
  Seven_Seg seven_seg_4 (
    .a(NumA_0[3]), .b(NumA_0[2]), .c(NumA_0[1]), .d(NumA_0[0]), .e(NumA_0[6]), .f(NumA_0[5]), .g(NumA_0[4]),
    .dp(1'b0));
  PullDown #(.Bits(7)) pulldown_87 (.out(NumA_0));
  PullDown #(.Bits(7)) pulldown_88 (.out(NumA_1));
  PullDown #(.Bits(7)) pulldown_89 (.out(NumA_0));
  PullDown #(.Bits(7)) pulldown_90 (.out(NumA_2));
  PullDown #(.Bits(7)) pulldown_91 (.out(NumA_1));
  PullDown #(.Bits(7)) pulldown_92 (.out(NumA_0));
  PullDown #(.Bits(7)) pulldown_93 (.out(NumA_3));
  PullDown #(.Bits(7)) pulldown_94 (.out(NumA_2));
  PullDown #(.Bits(7)) pulldown_95 (.out(NumA_1));
  PullDown #(.Bits(7)) pulldown_96 (.out(NumA_0));
  Seven_Seg seven_seg_5 (
    .a(Result_3[3]), .b(Result_3[2]), .c(Result_3[1]), .d(Result_3[0]), .e(Result_3[6]), .f(Result_3[5]),
    .g(Result_3[4]), .dp(1'b0));
  Comparator #(.Bits(4)) comparator_92 (.a(numB_count), .b(4'b0000), .gt(comparator_92_gt));  // open: eq, lt
  Seven_Seg seven_seg_6 (
    .a(NumB_3[3]), .b(NumB_3[2]), .c(NumB_3[1]), .d(NumB_3[0]), .e(NumB_3[6]), .f(NumB_3[5]), .g(NumB_3[4]),
    .dp(1'b0));
  and and_13 (and_13_out, ENTER, comparator_92_gt);
  RS_FF_AS rs_ff_as_6 (.S(CLEAR), .R(and_13_out), .Q(rs_ff_as_6_q));  // open: nQ
  Comparator #(.Bits(4)) comparator_93 (.a(count_out), .b(4'b0100), .gt(comparator_93_gt));  // open: eq, lt
  Comparator #(.Bits(4)) comparator_94 (.a(numB_count), .b(4'b0001), .eq(comparator_94_eq));  // open: gt, lt
  Comparator #(.Bits(4)) comparator_95 (.a(numB_count), .b(4'b0010), .eq(comparator_95_eq));  // open: gt, lt
  Comparator #(.Bits(4)) comparator_96 (.a(numB_count), .b(4'b0011), .eq(comparator_96_eq));  // open: gt, lt
  Comparator #(.Bits(4)) comparator_97 (.a(numB_count), .b(4'b0100), .eq(comparator_97_eq));  // open: gt, lt
  Seven_Seg seven_seg_7 (
    .a(Result_2[3]), .b(Result_2[2]), .c(Result_2[1]), .d(Result_2[0]), .e(Result_2[6]), .f(Result_2[5]),
    .g(Result_2[4]), .dp(1'b0));
  not not_3 (not_3_out, comparator_93_gt);
  and and_14 (and_14_out, comparator_94_eq, 1'b1);
  and and_15 (and_15_out, comparator_95_eq, 1'b1);
  and and_16 (and_16_out, comparator_96_eq, 1'b1);
  and and_17 (and_17_out, comparator_97_eq, 1'b1);
  Seven_Seg seven_seg_8 (
    .a(NumB_2[3]), .b(NumB_2[2]), .c(NumB_2[1]), .d(NumB_2[0]), .e(NumB_2[6]), .f(NumB_2[5]), .g(NumB_2[4]),
    .dp(1'b0));
  and and_18 (and_18_out, B, rs_ff_as_6_q, not_3_out);
  Delay #(.delayTime(2)) delay_9 (.in(CLEAR), .out(delay_9_out));
  Delay #(.delayTime(15)) delay_10 (.in(count_in), .out(delay_10_out));
  // Relay #(.Bits(7)) relay_91: pin names not known; wires that end beside it: and_14_out, Num2_0, and_15_out, 1'b0, NumB_0, 1'b0
  // Relay #(.poles(2), .Bits(7)) relay_92: pin names not known; wires that end beside it: Num2_0, Num2_1, NumB_1, NumB_0
  // Relay #(.poles(3), .Bits(7)) relay_93: pin names not known; wires that end beside it: and_16_out, Num2_0, Num2_1, Num2_2, 1'b0, NumB_2, NumB_1, NumB_0
  // Relay #(.poles(4), .Bits(7)) relay_94: pin names not known; wires that end beside it: and_17_out, Num2_0, Num2_1, Num2_2, Num2_3, 1'b0, NumB_3, NumB_2, NumB_1, NumB_0
  Delay #(.Bits(4), .delayTime(4)) delay_11 (.in(count_out), .out(delay_11_out));
  or or_17 (or_17_out, CLEAR, and_18_out);
  // RelayDT #(.Bits(4)) relaydt_3: pin names not known; wires that end beside it: CLEAR, 4'b0000, delay_11_out, 1'b0, relaydt_3_p5
  Register #(.Bits(4)) register_6 (.D(relaydt_3_p5), .C(relaydt_4_p5), .en(or_17_out), .Q(numB_count));
  // RelayDT relaydt_4: pin names not known; wires that end beside it: delay_9_out, CLEAR, delay_10_out, 1'b0, relaydt_4_p5
  PullDown #(.Bits(7)) pulldown_97 (.out(NumB_0));
  PullDown #(.Bits(7)) pulldown_98 (.out(NumB_1));
  PullDown #(.Bits(7)) pulldown_99 (.out(NumB_0));
  PullDown #(.Bits(7)) pulldown_100 (.out(NumB_2));
  PullDown #(.Bits(7)) pulldown_101 (.out(NumB_1));
  PullDown #(.Bits(7)) pulldown_102 (.out(NumB_0));
  PullDown #(.Bits(7)) pulldown_103 (.out(NumB_3));
  PullDown #(.Bits(7)) pulldown_104 (.out(NumB_2));
  PullDown #(.Bits(7)) pulldown_105 (.out(NumB_1));
  PullDown #(.Bits(7)) pulldown_106 (.out(NumB_0));
  Seven_Seg seven_seg_9 (
    .a(Result_1[3]), .b(Result_1[2]), .c(Result_1[1]), .d(Result_1[0]), .e(Result_1[6]), .f(Result_1[5]),
    .g(Result_1[4]), .dp(1'b0));
  Seven_Seg seven_seg_10 (
    .a(NumB_1[3]), .b(NumB_1[2]), .c(NumB_1[1]), .d(NumB_1[0]), .e(NumB_1[6]), .f(NumB_1[5]), .g(NumB_1[4]),
    .dp(1'b0));
  Seven_Seg seven_seg_11 (
    .a(Result_0[3]), .b(Result_0[2]), .c(Result_0[1]), .d(Result_0[0]), .e(Result_0[6]), .f(Result_0[5]),
    .g(Result_0[4]), .dp(1'b0));
  Seven_Seg seven_seg_12 (
    .a(NumB_0[3]), .b(NumB_0[2]), .c(NumB_0[1]), .d(NumB_0[0]), .e(NumB_0[6]), .f(NumB_0[5]), .g(NumB_0[4]),
    .dp(1'b0));
  Comparator #(.Bits(4)) comparator_98 (.a(numA_count), .b(4'b0000), .gt(comparator_98_gt));  // open: eq, lt
  or or_18 (count_res, plus, in_31, in_32, in_33);
  Comparator #(.Bits(4)) comparator_99 (.a(count_out), .b(4'b0100), .eq(comparator_99_eq));  // open: gt, lt
  and and_19 (and_19_out, count_res, comparator_98_gt);
  or or_19 (or_19_out, and_19_out, CLEAR);
  not not_4 (not_4_out, count_num2);
  Register register_7 (.D(count_res), .C(CLK), .en(or_19_out), .Q(register_7_q));
  and and_20 (and_20_out, comparator_99_eq, not_4_out, count_in);
  RS_FF_AS rs_ff_as_7 (.S(register_7_q), .R(CLEAR), .Q(count_num2));  // open: nQ
  or or_20 (or_20_out, and_20_out, CLEAR);
  Decoder decoder_1 (.sel(count_num2), .out_0(A), .out_1(B));
  Register #(.Bits(7)) register_8 (.D(A0), .C(CLK), .en(or_20_out), .Q(register_8_q));
  Register #(.Bits(7)) register_9 (.D(A1), .C(CLK), .en(or_20_out), .Q(register_9_q));
  Register #(.Bits(7)) register_10 (.D(A2), .C(CLK), .en(or_20_out), .Q(register_10_q));
  Register #(.Bits(7)) register_11 (.D(A3), .C(CLK), .en(or_20_out), .Q(register_11_q));
  Register #(.Bits(7)) register_12 (.D(A4), .C(CLK), .en(or_20_out), .Q(register_12_q));
  Register #(.Bits(7)) register_13 (.D(A5), .C(CLK), .en(or_20_out), .Q(register_13_q));
  Register #(.Bits(7)) register_14 (.D(A6), .C(CLK), .en(or_20_out), .Q(register_14_q));
  Register #(.Bits(7)) register_15 (.D(A7), .C(CLK), .en(or_20_out), .Q(register_15_q));
  Register #(.Bits(7)) register_16 (.D(A8), .C(CLK), .en(or_20_out), .Q(register_16_q));
  Register #(.Bits(7)) register_17 (.D(A9), .C(CLK), .en(or_20_out), .Q(register_17_q));
  and and_21 (and_21_out, _1, A);
  and and_22 (and_22_out, _4, A);
  and and_23 (and_23_out, _7, A);
  Seven_Seg seven_seg_13 (
    .a(Num1_3[3]), .b(Num1_3[2]), .c(Num1_3[1]), .d(Num1_3[0]), .e(Num1_3[6]), .f(Num1_3[5]), .g(Num1_3[4]),
    .dp(1'b0));
  _7448 _7448_5 (
    .pin1(1'b0), .pin2(1'b0), .pin3(and_21_out), .pin4(and_21_out), .pin5(and_21_out), .pin6(1'b0),
    .pin7(1'b1), .pin8(1'b0), .pin9(A1[6]), .pin10(A1[0]), .pin11(A1[1]), .pin12(A1[2]), .pin13(A1[3]),
    .pin14(A1[4]), .pin15(A1[5]), .pin16(1'b1));
  _7448 _7448_6 (
    .pin1(1'b0), .pin2(1'b1), .pin3(and_22_out), .pin4(and_22_out), .pin5(and_22_out), .pin6(1'b0),
    .pin7(1'b0), .pin8(1'b0), .pin9(A4[6]), .pin10(A4[0]), .pin11(A4[1]), .pin12(A4[2]), .pin13(A4[3]),
    .pin14(A4[4]), .pin15(A4[5]), .pin16(1'b1));
  _7448 _7448_7 (
    .pin1(1'b1), .pin2(1'b1), .pin3(and_23_out), .pin4(and_23_out), .pin5(and_23_out), .pin6(1'b0),
    .pin7(1'b1), .pin8(1'b0), .pin9(A7[6]), .pin10(A7[0]), .pin11(A7[1]), .pin12(A7[2]), .pin13(A7[3]),
    .pin14(A7[4]), .pin15(A7[5]), .pin16(1'b1));
  assign Num1_3 = register_8_q | register_9_q | register_10_q | register_11_q | register_12_q | register_13_q | register_14_q | register_15_q | register_16_q | register_17_q;  // Or or_21, 7 bits wide
  Comparator #(.Bits(4)) comparator_100 (.a(count_out), .b(4'b0011), .eq(comparator_100_eq));  // open: gt, lt
  and and_24 (and_24_out, comparator_100_eq, not_5_out, count_in);
  not not_5 (not_5_out, count_num2);
  or or_22 (or_22_out, and_24_out, CLEAR);
  Seven_Seg seven_seg_14 (.a(A4[3]), .b(A4[2]), .c(A4[1]), .d(A4[0]), .e(A4[6]), .f(A4[5]), .g(A4[4]), .dp(1'b0));
  Seven_Seg seven_seg_15 (.a(A7[3]), .b(A7[2]), .c(A7[1]), .d(A7[0]), .e(A7[6]), .f(A7[5]), .g(A7[4]), .dp(1'b0));
  Register #(.Bits(7)) register_18 (.D(A0), .C(CLK), .en(or_22_out), .Q(register_18_q));
  Register #(.Bits(7)) register_19 (.D(A1), .C(CLK), .en(or_22_out), .Q(register_19_q));
  Register #(.Bits(7)) register_20 (.D(A2), .C(CLK), .en(or_22_out), .Q(register_20_q));
  Register #(.Bits(7)) register_21 (.D(A3), .C(CLK), .en(or_22_out), .Q(register_21_q));
  Register #(.Bits(7)) register_22 (.D(A4), .C(CLK), .en(or_22_out), .Q(register_22_q));
  Register #(.Bits(7)) register_23 (.D(A5), .C(CLK), .en(or_22_out), .Q(register_23_q));
  Register #(.Bits(7)) register_24 (.D(A6), .C(CLK), .en(or_22_out), .Q(register_24_q));
  Register #(.Bits(7)) register_25 (.D(A7), .C(CLK), .en(or_22_out), .Q(register_25_q));
  Register #(.Bits(7)) register_26 (.D(A8), .C(CLK), .en(or_22_out), .Q(register_26_q));
  Register #(.Bits(7)) register_27 (.D(A9), .C(CLK), .en(or_22_out), .Q(register_27_q));
  Seven_Seg seven_seg_16 (.a(A1[3]), .b(A1[2]), .c(A1[1]), .d(A1[0]), .e(A1[6]), .f(A1[5]), .g(A1[4]), .dp(1'b0));
  Seven_Seg seven_seg_17 (
    .a(Num1_2[3]), .b(Num1_2[2]), .c(Num1_2[1]), .d(Num1_2[0]), .e(Num1_2[6]), .f(Num1_2[5]), .g(Num1_2[4]),
    .dp(1'b0));
  and and_25 (and_25_out, _0, A);
  and and_26 (and_26_out, _2, A);
  and and_27 (and_27_out, _5, A);
  and and_28 (and_28_out, _8, A);
  assign Num1_2 = register_18_q | register_19_q | register_20_q | register_21_q | register_22_q | register_23_q | register_24_q | register_25_q | register_26_q | register_27_q;  // Or or_23, 7 bits wide
  _7448 _7448_8 (
    .pin1(1'b0), .pin2(1'b0), .pin3(and_25_out), .pin4(and_25_out), .pin5(and_25_out), .pin6(1'b0),
    .pin7(1'b0), .pin8(1'b0), .pin9(A0[6]), .pin10(A0[0]), .pin11(A0[1]), .pin12(A0[2]), .pin13(A0[3]),
    .pin14(A0[4]), .pin15(A0[5]), .pin16(1'b1));
  _7448 _7448_9 (
    .pin1(1'b1), .pin2(1'b0), .pin3(and_26_out), .pin4(and_26_out), .pin5(and_26_out), .pin6(1'b0),
    .pin7(1'b0), .pin8(1'b0), .pin9(A2[6]), .pin10(A2[0]), .pin11(A2[1]), .pin12(A2[2]), .pin13(A2[3]),
    .pin14(A2[4]), .pin15(A2[5]), .pin16(1'b1));
  _7448 _7448_10 (
    .pin1(1'b0), .pin2(1'b1), .pin3(and_27_out), .pin4(and_27_out), .pin5(and_27_out), .pin6(1'b0),
    .pin7(1'b1), .pin8(1'b0), .pin9(A5[6]), .pin10(A5[0]), .pin11(A5[1]), .pin12(A5[2]), .pin13(A5[3]),
    .pin14(A5[4]), .pin15(A5[5]), .pin16(1'b1));
  _7448 _7448_11 (
    .pin1(1'b0), .pin2(1'b0), .pin3(and_28_out), .pin4(and_28_out), .pin5(and_28_out), .pin6(1'b1),
    .pin7(1'b0), .pin8(1'b0), .pin9(A8[6]), .pin10(A8[0]), .pin11(A8[1]), .pin12(A8[2]), .pin13(A8[3]),
    .pin14(A8[4]), .pin15(A8[5]), .pin16(1'b1));
  Comparator #(.Bits(4)) comparator_101 (.a(count_out), .b(4'b0010), .eq(comparator_101_eq));  // open: gt, lt
  not not_6 (not_6_out, count_num2);
  and and_29 (and_29_out, comparator_101_eq, not_6_out, count_in);
  or or_24 (or_24_out, and_29_out, CLEAR);
  Seven_Seg seven_seg_18 (.a(A0[3]), .b(A0[2]), .c(A0[1]), .d(A0[0]), .e(A0[6]), .f(A0[5]), .g(A0[4]), .dp(1'b0));
  Seven_Seg seven_seg_19 (.a(A2[3]), .b(A2[2]), .c(A2[1]), .d(A2[0]), .e(A2[6]), .f(A2[5]), .g(A2[4]), .dp(1'b0));
  Seven_Seg seven_seg_20 (.a(A5[3]), .b(A5[2]), .c(A5[1]), .d(A5[0]), .e(A5[6]), .f(A5[5]), .g(A5[4]), .dp(1'b0));
  Seven_Seg seven_seg_21 (.a(A8[3]), .b(A8[2]), .c(A8[1]), .d(A8[0]), .e(A8[6]), .f(A8[5]), .g(A8[4]), .dp(1'b0));
  Register #(.Bits(7)) register_28 (.D(A0), .C(CLK), .en(or_24_out), .Q(register_28_q));
  Register #(.Bits(7)) register_29 (.D(A1), .C(CLK), .en(or_24_out), .Q(register_29_q));
  Register #(.Bits(7)) register_30 (.D(A2), .C(CLK), .en(or_24_out), .Q(register_30_q));
  Register #(.Bits(7)) register_31 (.D(A3), .C(CLK), .en(or_24_out), .Q(register_31_q));
  Register #(.Bits(7)) register_32 (.D(A4), .C(CLK), .en(or_24_out), .Q(register_32_q));
  Register #(.Bits(7)) register_33 (.D(A5), .C(CLK), .en(or_24_out), .Q(register_33_q));
  Register #(.Bits(7)) register_34 (.D(A6), .C(CLK), .en(or_24_out), .Q(register_34_q));
  Register #(.Bits(7)) register_35 (.D(A7), .C(CLK), .en(or_24_out), .Q(register_35_q));
  Register #(.Bits(7)) register_36 (.D(A8), .C(CLK), .en(or_24_out), .Q(register_36_q));
  Register #(.Bits(7)) register_37 (.D(A9), .C(CLK), .en(or_24_out), .Q(register_37_q));
  Seven_Seg seven_seg_22 (
    .a(Num1_1[3]), .b(Num1_1[2]), .c(Num1_1[1]), .d(Num1_1[0]), .e(Num1_1[6]), .f(Num1_1[5]), .g(Num1_1[4]),
    .dp(1'b0));
  and and_30 (and_30_out, _3, A);
  and and_31 (and_31_out, _6, A);
  and and_32 (and_32_out, _9, A);
  assign Num1_1 = register_28_q | register_29_q | register_30_q | register_31_q | register_32_q | register_33_q | register_34_q | register_35_q | register_36_q | register_37_q;  // Or or_25, 7 bits wide
  _7448 _7448_12 (
    .pin1(1'b1), .pin2(1'b0), .pin3(and_30_out), .pin4(and_30_out), .pin5(and_30_out), .pin6(1'b0),
    .pin7(1'b1), .pin8(1'b0), .pin9(A3[6]), .pin10(A3[0]), .pin11(A3[1]), .pin12(A3[2]), .pin13(A3[3]),
    .pin14(A3[4]), .pin15(A3[5]), .pin16(1'b1));
  _7448 _7448_13 (
    .pin1(1'b1), .pin2(1'b1), .pin3(and_31_out), .pin4(and_31_out), .pin5(and_31_out), .pin6(1'b0),
    .pin7(1'b0), .pin8(1'b0), .pin9(A6[6]), .pin10(A6[0]), .pin11(A6[1]), .pin12(A6[2]), .pin13(A6[3]),
    .pin14(A6[4]), .pin15(A6[5]), .pin16(1'b1));
  _7448 _7448_14 (
    .pin1(1'b0), .pin2(1'b0), .pin3(and_32_out), .pin4(and_32_out), .pin5(and_32_out), .pin6(1'b1),
    .pin7(1'b1), .pin8(1'b0), .pin9(A9[6]), .pin10(A9[0]), .pin11(A9[1]), .pin12(A9[2]), .pin13(A9[3]),
    .pin14(A9[4]), .pin15(A9[5]), .pin16(1'b1));
  Comparator #(.Bits(4)) comparator_102 (.a(count_out), .b(4'b0001), .eq(comparator_102_eq));  // open: gt, lt
  not not_7 (not_7_out, count_num2);
  and and_33 (and_33_out, comparator_102_eq, not_7_out, count_in);
  or or_26 (or_26_out, and_33_out, CLEAR);
  Register #(.Bits(7)) register_38 (.D(A0), .C(CLK), .en(or_26_out), .Q(register_38_q));
  Register #(.Bits(7)) register_39 (.D(A1), .C(CLK), .en(or_26_out), .Q(register_39_q));
  Register #(.Bits(7)) register_40 (.D(A2), .C(CLK), .en(or_26_out), .Q(register_40_q));
  Register #(.Bits(7)) register_41 (.D(A3), .C(CLK), .en(or_26_out), .Q(register_41_q));
  Register #(.Bits(7)) register_42 (.D(A4), .C(CLK), .en(or_26_out), .Q(register_42_q));
  Register #(.Bits(7)) register_43 (.D(A5), .C(CLK), .en(or_26_out), .Q(register_43_q));
  Register #(.Bits(7)) register_44 (.D(A6), .C(CLK), .en(or_26_out), .Q(register_44_q));
  Register #(.Bits(7)) register_45 (.D(A7), .C(CLK), .en(or_26_out), .Q(register_45_q));
  Register #(.Bits(7)) register_46 (.D(A8), .C(CLK), .en(or_26_out), .Q(register_46_q));
  Register #(.Bits(7)) register_47 (.D(A9), .C(CLK), .en(or_26_out), .Q(register_47_q));
  Seven_Seg seven_seg_23 (.a(A3[3]), .b(A3[2]), .c(A3[1]), .d(A3[0]), .e(A3[6]), .f(A3[5]), .g(A3[4]), .dp(1'b0));
  Seven_Seg seven_seg_24 (.a(A6[3]), .b(A6[2]), .c(A6[1]), .d(A6[0]), .e(A6[6]), .f(A6[5]), .g(A6[4]), .dp(1'b0));
  Seven_Seg seven_seg_25 (.a(A9[3]), .b(A9[2]), .c(A9[1]), .d(A9[0]), .e(A9[6]), .f(A9[5]), .g(A9[4]), .dp(1'b0));
  Seven_Seg seven_seg_26 (
    .a(Num1_0[3]), .b(Num1_0[2]), .c(Num1_0[1]), .d(Num1_0[0]), .e(Num1_0[6]), .f(Num1_0[5]), .g(Num1_0[4]),
    .dp(1'b0));
  or or_27 (count_in, _9, _8, _7, _6, _5, _4, _3, _2, _1, _0);
  or or_28 (press_notzero, _9, _8, _7, _6, _5, _4, _3, _2, _1);
  and and_34 (and_34_out, count1, A, num1_zero);
  and and_35 (and_35_out, count1, B, num2_zero);
  assign Num1_0 = register_38_q | register_39_q | register_40_q | register_41_q | register_42_q | register_43_q | register_44_q | register_45_q | register_46_q | register_47_q;  // Or or_29, 7 bits wide
  or or_30 (or_30_out, and_34_out, and_35_out);
  and and_36 (and_36_out, or_30_out, press_notzero);
  or or_31 (or_31_out, and_36_out, press_notzero);
  or or_32 (or_32_out, and_36_out, CLEAR);
  Register register_48 (.D(and_36_out), .C(or_31_out), .en(1'b1), .Q(register_48_q));
  Comparator #(.Bits(4)) comparator_103 (
    .a(count_out), .b(4'b0001), .eq(comparator_103_eq), .lt(comparator_103_lt));  // open: gt
  Counter #(.Bits(4)) counter_2 (.en(1'b1), .C(or_32_out), .clr(CLEAR), .out(counter_2_out));  // open: ovf
  Comparator #(.Bits(4)) comparator_104 (.a(4'b0001), .b(counter_2_out), .eq(comparator_104_eq));  // open: gt, lt
  or or_33 (or_33_out, comparator_103_eq, comparator_103_lt);
  and and_37 (and_37_out, register_48_q, comparator_104_eq, or_33_out);
  Register #(.Bits(7)) register_49 (.D(Num1_0), .C(CLK), .en(1'b1), .Q(register_49_q));
  Register #(.Bits(7)) register_50 (.D(Num2_0), .C(CLK), .en(1'b1), .Q(register_50_q));
  not not_8 (not_8_out, B);
  Comparator #(.Bits(7)) comparator_105 (.a(register_49_q), .b(7'b1101111), .eq(num1_zero));  // open: gt, lt
  Comparator #(.Bits(4)) comparator_106 (.a(count_out), .b(4'b0001), .eq(count1));  // open: gt, lt
  Comparator #(.Bits(7)) comparator_107 (.a(register_50_q), .b(7'b1101111), .eq(num2_zero));  // open: gt, lt
  Delay #(.delayTime(8)) delay_12 (.in(count_in), .out(delay_12_out));
  and and_38 (and_38_out, count_res, not_8_out);
  // Relay #(.relayNormallyClosed("true")) relay_95: pin names not known; wires that end beside it: and_37_out, delay_12_out, 1'b0, relay_95_p4
  Comparator #(.Bits(4)) comparator_108 (.a(count_out), .b(4'b0100), .eq(comparator_108_eq));  // open: gt, lt
  and and_39 (and_39_out, num1_zero, count1, _0);
  and and_40 (and_40_out, num2_zero, count1, _0);
  PullDown pulldown_107 (.out(relay_95_p4));
  or or_34 (or_34_out, relay_95_p4, and_38_out, CLEAR);
  Delay delay_13 (.in(or_34_out), .out(delay_13_out));
  and and_41 (and_41_out, comparator_108_eq, count_in);
  or or_35 (or_35_out, and_39_out, and_40_out);
  or or_36 (or_36_out, and_41_out, CLEAR);
  Delay #(.delayTime(8)) delay_14 (.in(or_35_out), .out(delay_14_out));
  or or_37 (or_37_out, and_38_out, CLEAR);
  // Relay #(.relayNormallyClosed("true")) relay_96: pin names not known; wires that end beside it: delay_14_out, delay_13_out, 1'b0, relay_96_p4
  PullDown pulldown_108 (.out(relay_96_p4));
  Register #(.Bits(7)) register_51 (.D(B0), .C(CLK), .en(or_36_out), .Q(register_51_q));
  Register #(.Bits(7)) register_52 (.D(B1), .C(CLK), .en(or_36_out), .Q(register_52_q));
  Register #(.Bits(7)) register_53 (.D(B2), .C(CLK), .en(or_36_out), .Q(register_53_q));
  Register #(.Bits(7)) register_54 (.D(B3), .C(CLK), .en(or_36_out), .Q(register_54_q));
  Register #(.Bits(7)) register_55 (.D(B4), .C(CLK), .en(or_36_out), .Q(register_55_q));
  Register #(.Bits(7)) register_56 (.D(B5), .C(CLK), .en(or_36_out), .Q(register_56_q));
  Register #(.Bits(7)) register_57 (.D(B6), .C(CLK), .en(or_36_out), .Q(register_57_q));
  Register #(.Bits(7)) register_58 (.D(B7), .C(CLK), .en(or_36_out), .Q(register_58_q));
  Register #(.Bits(7)) register_59 (.D(B8), .C(CLK), .en(or_36_out), .Q(register_59_q));
  Register #(.Bits(7)) register_60 (.D(B9), .C(CLK), .en(or_36_out), .Q(register_60_q));
  and and_42 (and_42_out, _1, B);
  and and_43 (and_43_out, _4, B);
  and and_44 (and_44_out, _7, B);
  Counter #(.Bits(4)) counter_3 (.en(1'b1), .C(relay_96_p4), .clr(or_37_out), .out(count_out));  // open: ovf
  _7448 _7448_15 (
    .pin1(1'b0), .pin2(1'b0), .pin3(and_42_out), .pin4(and_42_out), .pin5(and_42_out), .pin6(1'b0),
    .pin7(1'b1), .pin8(1'b0), .pin9(B1[6]), .pin10(B1[0]), .pin11(B1[1]), .pin12(B1[2]), .pin13(B1[3]),
    .pin14(B1[4]), .pin15(B1[5]), .pin16(1'b1));
  _7448 _7448_16 (
    .pin1(1'b0), .pin2(1'b1), .pin3(and_43_out), .pin4(and_43_out), .pin5(and_43_out), .pin6(1'b0),
    .pin7(1'b0), .pin8(1'b0), .pin9(B4[6]), .pin10(B4[0]), .pin11(B4[1]), .pin12(B4[2]), .pin13(B4[3]),
    .pin14(B4[4]), .pin15(B4[5]), .pin16(1'b1));
  _7448 _7448_17 (
    .pin1(1'b1), .pin2(1'b1), .pin3(and_44_out), .pin4(and_44_out), .pin5(and_44_out), .pin6(1'b0),
    .pin7(1'b1), .pin8(1'b0), .pin9(B7[6]), .pin10(B7[0]), .pin11(B7[1]), .pin12(B7[2]), .pin13(B7[3]),
    .pin14(B7[4]), .pin15(B7[5]), .pin16(1'b1));
  Seven_Seg seven_seg_27 (
    .a(Num2_3[3]), .b(Num2_3[2]), .c(Num2_3[1]), .d(Num2_3[0]), .e(Num2_3[6]), .f(Num2_3[5]), .g(Num2_3[4]),
    .dp(1'b0));
  assign Num2_3 = register_51_q | register_52_q | register_53_q | register_54_q | register_55_q | register_56_q | register_57_q | register_58_q | register_59_q | register_60_q;  // Or or_38, 7 bits wide
  Comparator #(.Bits(4)) comparator_109 (.a(count_out), .b(4'b0011), .eq(comparator_109_eq));  // open: gt, lt
  and and_45 (and_45_out, comparator_109_eq, count_in);
  Seven_Seg seven_seg_28 (.a(B1[3]), .b(B1[2]), .c(B1[1]), .d(B1[0]), .e(B1[6]), .f(B1[5]), .g(B1[4]), .dp(1'b0));
  Seven_Seg seven_seg_29 (.a(B4[3]), .b(B4[2]), .c(B4[1]), .d(B4[0]), .e(B4[6]), .f(B4[5]), .g(B4[4]), .dp(1'b0));
  Seven_Seg seven_seg_30 (.a(B7[3]), .b(B7[2]), .c(B7[1]), .d(B7[0]), .e(B7[6]), .f(B7[5]), .g(B7[4]), .dp(1'b0));
  or or_39 (or_39_out, and_45_out, CLEAR);
  Register #(.Bits(7)) register_61 (.D(B0), .C(CLK), .en(or_39_out), .Q(register_61_q));
  Register #(.Bits(7)) register_62 (.D(B1), .C(CLK), .en(or_39_out), .Q(register_62_q));
  Register #(.Bits(7)) register_63 (.D(B2), .C(CLK), .en(or_39_out), .Q(register_63_q));
  Register #(.Bits(7)) register_64 (.D(B3), .C(CLK), .en(or_39_out), .Q(register_64_q));
  Register #(.Bits(7)) register_65 (.D(B4), .C(CLK), .en(or_39_out), .Q(register_65_q));
  Register #(.Bits(7)) register_66 (.D(B5), .C(CLK), .en(or_39_out), .Q(register_66_q));
  Register #(.Bits(7)) register_67 (.D(B6), .C(CLK), .en(or_39_out), .Q(register_67_q));
  Register #(.Bits(7)) register_68 (.D(B7), .C(CLK), .en(or_39_out), .Q(register_68_q));
  Register #(.Bits(7)) register_69 (.D(B8), .C(CLK), .en(or_39_out), .Q(register_69_q));
  Register #(.Bits(7)) register_70 (.D(B9), .C(CLK), .en(or_39_out), .Q(register_70_q));
  Seven_Seg seven_seg_31 (
    .a(Num2_2[3]), .b(Num2_2[2]), .c(Num2_2[1]), .d(Num2_2[0]), .e(Num2_2[6]), .f(Num2_2[5]), .g(Num2_2[4]),
    .dp(1'b0));
  and and_46 (and_46_out, _0, B);
  and and_47 (and_47_out, _2, B);
  and and_48 (and_48_out, _5, B);
  and and_49 (and_49_out, _8, B);
  assign Num2_2 = register_61_q | register_62_q | register_63_q | register_64_q | register_65_q | register_66_q | register_67_q | register_68_q | register_69_q | register_70_q;  // Or or_40, 7 bits wide
  _7448 _7448_18 (
    .pin1(1'b0), .pin2(1'b0), .pin3(and_46_out), .pin4(and_46_out), .pin5(and_46_out), .pin6(1'b0),
    .pin7(1'b0), .pin8(1'b0), .pin9(B0[6]), .pin10(B0[0]), .pin11(B0[1]), .pin12(B0[2]), .pin13(B0[3]),
    .pin14(B0[4]), .pin15(B0[5]), .pin16(1'b1));
  _7448 _7448_19 (
    .pin1(1'b1), .pin2(1'b0), .pin3(and_47_out), .pin4(and_47_out), .pin5(and_47_out), .pin6(1'b0),
    .pin7(1'b0), .pin8(1'b0), .pin9(B2[6]), .pin10(B2[0]), .pin11(B2[1]), .pin12(B2[2]), .pin13(B2[3]),
    .pin14(B2[4]), .pin15(B2[5]), .pin16(1'b1));
  _7448 _7448_20 (
    .pin1(1'b0), .pin2(1'b1), .pin3(and_48_out), .pin4(and_48_out), .pin5(and_48_out), .pin6(1'b0),
    .pin7(1'b1), .pin8(1'b0), .pin9(B5[6]), .pin10(B5[0]), .pin11(B5[1]), .pin12(B5[2]), .pin13(B5[3]),
    .pin14(B5[4]), .pin15(B5[5]), .pin16(1'b1));
  _7448 _7448_21 (
    .pin1(1'b0), .pin2(1'b0), .pin3(and_49_out), .pin4(and_49_out), .pin5(and_49_out), .pin6(1'b1),
    .pin7(1'b0), .pin8(1'b0), .pin9(B8[6]), .pin10(B8[0]), .pin11(B8[1]), .pin12(B8[2]), .pin13(B8[3]),
    .pin14(B8[4]), .pin15(B8[5]), .pin16(1'b1));
  Comparator #(.Bits(4)) comparator_110 (.a(count_out), .b(4'b0010), .eq(comparator_110_eq));  // open: gt, lt
  and and_50 (and_50_out, comparator_110_eq, count_in);
  or or_41 (or_41_out, and_50_out, CLEAR);
  Seven_Seg seven_seg_32 (.a(B0[3]), .b(B0[2]), .c(B0[1]), .d(B0[0]), .e(B0[6]), .f(B0[5]), .g(B0[4]), .dp(1'b0));
  Seven_Seg seven_seg_33 (.a(B2[3]), .b(B2[2]), .c(B2[1]), .d(B2[0]), .e(B2[6]), .f(B2[5]), .g(B2[4]), .dp(1'b0));
  Seven_Seg seven_seg_34 (.a(B5[3]), .b(B5[2]), .c(B5[1]), .d(B5[0]), .e(B5[6]), .f(B5[5]), .g(B5[4]), .dp(1'b0));
  Seven_Seg seven_seg_35 (.a(B8[3]), .b(B8[2]), .c(B8[1]), .d(B8[0]), .e(B8[6]), .f(B8[5]), .g(B8[4]), .dp(1'b0));
  Register #(.Bits(7)) register_71 (.D(B0), .C(CLK), .en(or_41_out), .Q(register_71_q));
  Register #(.Bits(7)) register_72 (.D(B1), .C(CLK), .en(or_41_out), .Q(register_72_q));
  Register #(.Bits(7)) register_73 (.D(B2), .C(CLK), .en(or_41_out), .Q(register_73_q));
  Register #(.Bits(7)) register_74 (.D(B3), .C(CLK), .en(or_41_out), .Q(register_74_q));
  Register #(.Bits(7)) register_75 (.D(B4), .C(CLK), .en(or_41_out), .Q(register_75_q));
  Register #(.Bits(7)) register_76 (.D(B5), .C(CLK), .en(or_41_out), .Q(register_76_q));
  Register #(.Bits(7)) register_77 (.D(B6), .C(CLK), .en(or_41_out), .Q(register_77_q));
  Register #(.Bits(7)) register_78 (.D(B7), .C(CLK), .en(or_41_out), .Q(register_78_q));
  Register #(.Bits(7)) register_79 (.D(B8), .C(CLK), .en(or_41_out), .Q(register_79_q));
  Register #(.Bits(7)) register_80 (.D(B9), .C(CLK), .en(or_41_out), .Q(register_80_q));
  Seven_Seg seven_seg_36 (
    .a(Num2_1[3]), .b(Num2_1[2]), .c(Num2_1[1]), .d(Num2_1[0]), .e(Num2_1[6]), .f(Num2_1[5]), .g(Num2_1[4]),
    .dp(1'b0));
  assign Num2_1 = register_71_q | register_72_q | register_73_q | register_74_q | register_75_q | register_76_q | register_77_q | register_78_q | register_79_q | register_80_q;  // Or or_42, 7 bits wide
  and and_51 (and_51_out, _3, B);
  and and_52 (and_52_out, _6, B);
  and and_53 (and_53_out, _9, B);
  _7448 _7448_22 (
    .pin1(1'b1), .pin2(1'b0), .pin3(and_51_out), .pin4(and_51_out), .pin5(and_51_out), .pin6(1'b0),
    .pin7(1'b1), .pin8(1'b0), .pin9(B3[6]), .pin10(B3[0]), .pin11(B3[1]), .pin12(B3[2]), .pin13(B3[3]),
    .pin14(B3[4]), .pin15(B3[5]), .pin16(1'b1));
  _7448 _7448_23 (
    .pin1(1'b1), .pin2(1'b1), .pin3(and_52_out), .pin4(and_52_out), .pin5(and_52_out), .pin6(1'b0),
    .pin7(1'b0), .pin8(1'b0), .pin9(B6[6]), .pin10(B6[0]), .pin11(B6[1]), .pin12(B6[2]), .pin13(B6[3]),
    .pin14(B6[4]), .pin15(B6[5]), .pin16(1'b1));
  _7448 _7448_24 (
    .pin1(1'b0), .pin2(1'b0), .pin3(and_53_out), .pin4(and_53_out), .pin5(and_53_out), .pin6(1'b1),
    .pin7(1'b1), .pin8(1'b0), .pin9(B9[6]), .pin10(B9[0]), .pin11(B9[1]), .pin12(B9[2]), .pin13(B9[3]),
    .pin14(B9[4]), .pin15(B9[5]), .pin16(1'b1));
  Comparator #(.Bits(4)) comparator_111 (.a(count_out), .b(4'b0001), .eq(comparator_111_eq));  // open: gt, lt
  and and_54 (and_54_out, comparator_111_eq, count_in);
  or or_43 (or_43_out, and_54_out, CLEAR);
  Register #(.Bits(7)) register_81 (.D(B0), .C(CLK), .en(or_43_out), .Q(register_81_q));
  Register #(.Bits(7)) register_82 (.D(B1), .C(CLK), .en(or_43_out), .Q(register_82_q));
  Register #(.Bits(7)) register_83 (.D(B2), .C(CLK), .en(or_43_out), .Q(register_83_q));
  Register #(.Bits(7)) register_84 (.D(B3), .C(CLK), .en(or_43_out), .Q(register_84_q));
  Register #(.Bits(7)) register_85 (.D(B4), .C(CLK), .en(or_43_out), .Q(register_85_q));
  Register #(.Bits(7)) register_86 (.D(B5), .C(CLK), .en(or_43_out), .Q(register_86_q));
  Register #(.Bits(7)) register_87 (.D(B6), .C(CLK), .en(or_43_out), .Q(register_87_q));
  Register #(.Bits(7)) register_88 (.D(B7), .C(CLK), .en(or_43_out), .Q(register_88_q));
  Register #(.Bits(7)) register_89 (.D(B8), .C(CLK), .en(or_43_out), .Q(register_89_q));
  Register #(.Bits(7)) register_90 (.D(B9), .C(CLK), .en(or_43_out), .Q(register_90_q));
  Seven_Seg seven_seg_37 (.a(B3[3]), .b(B3[2]), .c(B3[1]), .d(B3[0]), .e(B3[6]), .f(B3[5]), .g(B3[4]), .dp(1'b0));
  Seven_Seg seven_seg_38 (.a(B6[3]), .b(B6[2]), .c(B6[1]), .d(B6[0]), .e(B6[6]), .f(B6[5]), .g(B6[4]), .dp(1'b0));
  Seven_Seg seven_seg_39 (.a(B9[3]), .b(B9[2]), .c(B9[1]), .d(B9[0]), .e(B9[6]), .f(B9[5]), .g(B9[4]), .dp(1'b0));
  Seven_Seg seven_seg_40 (
    .a(Num2_0[3]), .b(Num2_0[2]), .c(Num2_0[1]), .d(Num2_0[0]), .e(Num2_0[6]), .f(Num2_0[5]), .g(Num2_0[4]),
    .dp(1'b0));
  assign Num2_0 = register_81_q | register_82_q | register_83_q | register_84_q | register_85_q | register_86_q | register_87_q | register_88_q | register_89_q | register_90_q;  // Or or_44, 7 bits wide

  // Other names for the same wires on the sheet: result3[6:0] = Result_3; result2[6:0] = Result_2;
  //   result1[6:0] = Result_1; result0[6:0] = Result_0; Addition = plus; Division = in_33; err = ERROR;
  //   Multiplication = in_32; NumA0[6:0] = NumA_0; NumA1[6:0] = NumA_1; NumA2[6:0] = NumA_2; NumA3[6:0] = NumA_3;
  //   NumB0[6:0] = NumB_0; NumB1[6:0] = NumB_1; NumB2[6:0] = NumB_2; NumB3[6:0] = NumB_3; Substraction = in_31

  // Notes on the sheet:
  //   CLK: Hz: 10
  //   4-Number Digits
  //   5-Math Operation
  //   3-Number Display
  //   6-Display Result
  //   3.1-NumberA Display
  //   3.2-NumberB Display
  //   2.2-Number Register
  //   1.1-Number A
  //   2.1-Check If Digit0 Zero
  //   1.2-Number B
endmodule

/* Code of operation:
module operation (input [3:0] numA0,
	input [3:0] numA1,
	input [3:0] numA2,
	input [3:0] numA3,
	input [3:0] numB0,
	input [3:0] numB1,
	input [3:0] numB2,
	input [3:0] numB3,
	input [2:0] operation,
	input enter,
	input clr,
	output reg error,
	output reg [3:0] result3,
	output reg [3:0] result2,
	output reg [3:0] result1,
	output reg [3:0] result0,
	output reg negative
);
	reg [15:0] numA;
	reg [15:0] numB;
	reg [15:0] result;
	reg [31:0] temp;

initial begin
	result <= 0;
	result3 <= 0;
	result2 <= 0;
	result1 <= 0;
	result0 <= 0;
	numA <= 0;
	numB <= 0;
	temp <= 0;
	error <= 0;
	negative <= 0;
end

always@(posedge clr) begin
	result <= 0;
	result3 <= 0;
	result2 <= 0;
	result1 <= 0;
	result0 <= 0;
	numA <= 0;
	numB <= 0;
	temp <= 0;
	error <= 0;
	negative <= 0;
end

always@(posedge enter) begin
	negative = 0;
	numA = (numA3 * 1000) + (numA2 *100) + (numA1 * 10) + numA0;
	numB = (numB3 * 1000) + (numB2 *100) + (numB1 * 10) + numB0;

	case(operation)
	   3'b001: begin
		result = numA + numB;
		if (result > 9999) begin
		   result <= 0;
		   result3 <= 0;
		   result2 <= 0;
		   result1 <= 0;
		   result0 <= 0;
		   error <= 1;
		end else begin
		   error <= 0;
		   result0 = result % 10;
		   result1 = (result / 10) % 10;
		   result2 = (result / 100) % 10;
		   result3 = (result / 1000) % 10;
		end
	   end
	   3'b010: begin
		if (numB > numA) begin
		   result = numB - numA;
		   negative = 1;
		end else begin
		   result = numA - numB;
		end
		error <= 0;
		result0 = result % 10;
		result1 = (result / 10) % 10;
		result2 = (result / 100) % 10;
		result3 = (result / 1000) % 10;
	   end
	   3'b011: begin
		temp = numA * numB;
		if (temp > 9999) begin
		   result <= 0;
		   result3 <= 0;
		   result2 <= 0;
		   result1 <= 0;
		   result0 <= 0;
		   error <= 1;
		end else begin
		   error <= 0;
		   result = temp;
		   result0 = result % 10;
		   result1 = (result / 10) % 10;
		   result2 = (result / 100) % 10;
		   result3 = (result / 1000) % 10;
		end
	   end
	   3'b100: begin
		if (numB != 0) begin
		   result = numA / numB;
		   error <= 0;
		end else begin
		   result <= 0;
		   error <= 1;
		end
		result0 = result % 10;
		result1 = (result / 10) % 10;
		result2 = (result / 100) % 10;
		result3 = (result / 1000) % 10;
	   end
	endcase
end
endmodule
*/
